// Logisim project Alu.circ as structural Verilog: 8 circuits, main circuit main
module main (
  input  [2:0] in_1,
  input  [31:0] A,
  input  [31:0] B,
  output [31:0] salida,
  output zero,
  output overflow
);

  Alu32bits alu32bits_1 (.Salida(salida), .zero(zero), .Overflow(overflow), .A(A), .B(B), .Select(in_1));
endmodule

module Alu1bits (
  input  Carry_int,
  input  A,
  input  B,
  input  SLT,
  input  [2:0] Selector,
  input  Binvert,
  output Salida,
  output Carry_out
);

  wire and_1_out, multiplexer_1_out, not_1_out, not_2_out, or_1_out, sumador_1_salida, undriven;

  not not_1 (not_1_out, B);
  or or_1 (or_1_out, A, B);
  and and_1 (and_1_out, A, B);
  Multiplexer multiplexer_1 (.in0(B), .in1(not_1_out), .out(multiplexer_1_out), .sel(Binvert), .en(undriven));
  not not_2 (not_2_out, or_1_out);
  sumador sumador_1 (.A(A), .B(multiplexer_1_out), .Cin(Carry_int), .Salida(sumador_1_salida), .Cout(Carry_out));
  Multiplexer #(.select(3), .enable("false")) multiplexer_2 (
    .in0(sumador_1_salida), .in1(sumador_1_salida), .in2(SLT), .in4(and_1_out), .in5(not_2_out),
    .in6(or_1_out), .out(Salida), .sel(Selector));  // open: in3, in7
endmodule

module sumador (
  input  A,
  input  B,
  input  Cin,
  output Salida,
  output Cout
);

  wire and_1_out, and_2_out, and_3_out, and_4_out, and_5_out, and_6_out, and_7_out, not_1_out, not_2_out,
       not_3_out, not_4_out, not_5_out, not_6_out;

  not not_1 (not_1_out, A);
  not not_2 (not_2_out, B);
  not not_3 (not_3_out, A);
  not not_4 (not_4_out, Cin);
  not not_5 (not_5_out, B);
  not not_6 (not_6_out, Cin);
  and and_1 (and_1_out, B, Cin);
  and and_2 (and_2_out, A, Cin);
  and and_3 (and_3_out, A, B);
  and and_4 (and_4_out, not_1_out, not_2_out, Cin);
  and and_5 (and_5_out, not_3_out, B, not_4_out);
  and and_6 (and_6_out, A, not_5_out, not_6_out);
  and and_7 (and_7_out, A, B, Cin);
  or or_1 (Cout, and_1_out, and_2_out, and_3_out);
  or or_2 (Salida, and_4_out, and_5_out, and_6_out, and_7_out);
endmodule

module sumadorOverFlow (
  input  A,
  input  B,
  input  Cin,
  output Salida,
  output Cout,
  output Over_flow
);

  wire and_1_out, and_2_out, and_3_out, and_4_out, and_5_out, and_6_out, and_7_out, and_8_out, and_9_out,
       not_1_out, not_2_out, not_3_out, not_4_out, not_5_out, not_6_out, not_7_out;

  not not_1 (not_1_out, A);
  not not_2 (not_2_out, B);
  not not_3 (not_3_out, A);
  not not_4 (not_4_out, Cin);
  not not_5 (not_5_out, B);
  not not_6 (not_6_out, Cin);
  and and_1 (and_1_out, B, Cin);
  and and_2 (and_2_out, A, Cin);
  and and_3 (and_3_out, A, B);
  and and_4 (and_4_out, not_1_out, not_2_out, Cin);
  and and_5 (and_5_out, not_3_out, B, not_4_out);
  and and_6 (and_6_out, A, not_5_out, not_6_out);
  and and_7 (and_7_out, A, B, Cin);
  or or_1 (Cout, and_1_out, and_2_out, and_3_out);
  or or_2 (Salida, and_4_out, and_5_out, and_6_out, and_7_out);
  not not_7 (not_7_out, Cout);
  and and_8 (and_8_out, Cin, not_7_out);
  and and_9 (and_9_out, not_4_out, Cout);
  or or_3 (Over_flow, and_8_out, and_9_out);
endmodule

module Alu1bitsOverFlow (
  input  Carry_int,
  input  A,
  input  B,
  input  SLT,
  input  [2:0] Selector,
  input  Binvert,
  output Salida,
  output signo,
  output Carry_out,
  output overflow
);

  wire and_1_out, multiplexer_1_out, not_1_out, not_2_out, or_1_out, sumadoroverflow_1_salida, undriven;

  not not_1 (not_1_out, B);
  Multiplexer multiplexer_1 (.in0(B), .in1(not_1_out), .out(multiplexer_1_out), .sel(Binvert), .en(undriven));
  or or_1 (or_1_out, A, B);
  not not_2 (not_2_out, or_1_out);
  and and_1 (and_1_out, A, B);
  sumadorOverFlow sumadoroverflow_1 (
    .A(A), .B(multiplexer_1_out), .Cin(Carry_int), .Salida(sumadoroverflow_1_salida), .Cout(Carry_out),
    .Over_flow(overflow));
  Multiplexer #(.select(3), .enable("false")) multiplexer_2 (
    .in0(sumadoroverflow_1_salida), .in1(sumadoroverflow_1_salida), .in2(SLT), .in4(and_1_out),
    .in5(not_2_out), .in6(or_1_out), .out(Salida), .sel(Selector));  // open: in3, in7
  signo signo_1 (.A(A), .B(B), .Cin(Carry_int), .Sum(sumadoroverflow_1_salida), .Cout(Carry_out), .S(signo));
endmodule

module signo (
  input  A,
  input  B,
  input  Cin,
  input  Sum,
  input  Cout,
  output S
);

  wire and_1_out, and_2_out, and_3_out, and_4_out, not_1_out, not_2_out, not_3_out, not_4_out, not_5_out,
       not_6_out, not_7_out, not_8_out, not_9_out;

  not not_1 (not_1_out, A);
  not not_2 (not_2_out, B);
  not not_3 (not_3_out, Cin);
  not not_4 (not_4_out, Cout);
  not not_5 (not_5_out, B);
  not not_6 (not_6_out, Cin);
  not not_7 (not_7_out, B);
  not not_8 (not_8_out, Cin);
  not not_9 (not_9_out, Cout);
  and and_1 (and_1_out, not_1_out, not_2_out, Sum, not_3_out, not_4_out);
  and and_2 (and_2_out, A, not_5_out, Cout, not_6_out);
  and and_3 (and_3_out, A, not_7_out, Sum, Cout);
  and and_4 (and_4_out, A, B, Sum, not_8_out, not_9_out);
  or or_1 (S, and_1_out, and_2_out, and_3_out, and_4_out);
endmodule

// Alu
module Alu32bits (
  input  [2:0] Select,
  input  [31:0] A,
  input  [31:0] B,
  output [31:0] Salida,
  output zero,
  output Overflow
);

  wire alu1bits_1_carry_out, alu1bits_2_carry_out, alu1bits_3_carry_out, alu1bits_4_carry_out,
       alu1bits_5_carry_out, alu1bits_6_carry_out, alu1bits_7_carry_out, alu1bits_8_carry_out,
       alu1bits_9_carry_out, alu1bits_10_carry_out, alu1bits_11_carry_out, alu1bits_12_carry_out,
       alu1bits_13_carry_out, alu1bits_14_carry_out, alu1bits_15_carry_out, alu1bits_16_carry_out,
       alu1bits_17_carry_out, alu1bits_18_carry_out, alu1bits_19_carry_out, alu1bits_20_carry_out,
       alu1bits_21_carry_out, alu1bits_22_carry_out, alu1bits_23_carry_out, alu1bits_24_carry_out,
       alu1bits_25_carry_out, alu1bits_26_carry_out, alu1bits_27_carry_out, alu1bits_28_carry_out,
       alu1bits_29_carry_out, alu1bits_30_carry_out, alu1bits_31_carry_out, alu1bitsoverflow_1_signo,
       multiplexer_1_out, or_1_out;

  Alu1bits alu1bits_1 (
    .Carry_int(multiplexer_1_out), .A(A[0]), .B(B[0]), .SLT(alu1bitsoverflow_1_signo),
    .Binvert(multiplexer_1_out), .Salida(Salida[0]), .Selector(Select), .Carry_out(alu1bits_1_carry_out));
  Alu1bits alu1bits_2 (
    .Carry_int(alu1bits_1_carry_out), .A(A[1]), .B(B[1]), .SLT(1'b0), .Binvert(multiplexer_1_out),
    .Salida(Salida[1]), .Selector(Select), .Carry_out(alu1bits_2_carry_out));
  Alu1bits alu1bits_3 (
    .Carry_int(alu1bits_2_carry_out), .A(A[2]), .B(B[2]), .SLT(1'b0), .Binvert(multiplexer_1_out),
    .Salida(Salida[2]), .Selector(Select), .Carry_out(alu1bits_3_carry_out));
  Alu1bits alu1bits_4 (
    .Carry_int(alu1bits_3_carry_out), .A(A[3]), .B(B[3]), .SLT(1'b0), .Binvert(multiplexer_1_out),
    .Salida(Salida[3]), .Selector(Select), .Carry_out(alu1bits_4_carry_out));
  Alu1bits alu1bits_5 (
    .Carry_int(alu1bits_4_carry_out), .A(A[4]), .B(B[4]), .SLT(1'b0), .Binvert(multiplexer_1_out),
    .Salida(Salida[4]), .Selector(Select), .Carry_out(alu1bits_5_carry_out));
  Alu1bits alu1bits_6 (
    .Carry_int(alu1bits_5_carry_out), .A(A[5]), .B(B[5]), .SLT(1'b0), .Binvert(multiplexer_1_out),
    .Salida(Salida[5]), .Selector(Select), .Carry_out(alu1bits_6_carry_out));
  Alu1bits alu1bits_7 (
    .Carry_int(alu1bits_6_carry_out), .A(A[6]), .B(B[6]), .SLT(1'b0), .Binvert(multiplexer_1_out),
    .Salida(Salida[6]), .Selector(Select), .Carry_out(alu1bits_7_carry_out));
  Alu1bits alu1bits_8 (
    .Carry_int(alu1bits_7_carry_out), .A(A[7]), .B(B[7]), .SLT(1'b0), .Binvert(multiplexer_1_out),
    .Salida(Salida[7]), .Selector(Select), .Carry_out(alu1bits_8_carry_out));
  Alu1bits alu1bits_9 (
    .Carry_int(alu1bits_8_carry_out), .A(A[8]), .B(B[8]), .SLT(1'b0), .Binvert(multiplexer_1_out),
    .Salida(Salida[8]), .Selector(Select), .Carry_out(alu1bits_9_carry_out));
  Alu1bits alu1bits_10 (
    .Carry_int(alu1bits_9_carry_out), .A(A[9]), .B(B[9]), .SLT(1'b0), .Binvert(multiplexer_1_out),
    .Salida(Salida[9]), .Selector(Select), .Carry_out(alu1bits_10_carry_out));
  Alu1bits alu1bits_11 (
    .Carry_int(alu1bits_10_carry_out), .A(A[10]), .B(B[10]), .SLT(1'b0), .Binvert(multiplexer_1_out),
    .Salida(Salida[10]), .Selector(Select), .Carry_out(alu1bits_11_carry_out));
  Alu1bits alu1bits_12 (
    .Carry_int(alu1bits_11_carry_out), .A(A[11]), .B(B[11]), .SLT(1'b0), .Binvert(multiplexer_1_out),
    .Salida(Salida[11]), .Selector(Select), .Carry_out(alu1bits_12_carry_out));
  Alu1bits alu1bits_13 (
    .Carry_int(alu1bits_12_carry_out), .A(A[12]), .B(B[12]), .SLT(1'b0), .Binvert(multiplexer_1_out),
    .Salida(Salida[12]), .Selector(Select), .Carry_out(alu1bits_13_carry_out));
  Alu1bits alu1bits_14 (
    .Carry_int(alu1bits_13_carry_out), .A(A[13]), .B(B[13]), .SLT(1'b0), .Binvert(multiplexer_1_out),
    .Salida(Salida[13]), .Selector(Select), .Carry_out(alu1bits_14_carry_out));
  Alu1bits alu1bits_15 (
    .Carry_int(alu1bits_14_carry_out), .A(A[14]), .B(B[14]), .SLT(1'b0), .Binvert(multiplexer_1_out),
    .Salida(Salida[14]), .Selector(Select), .Carry_out(alu1bits_15_carry_out));
  Alu1bits alu1bits_16 (
    .Carry_int(alu1bits_15_carry_out), .A(A[15]), .B(B[15]), .SLT(1'b0), .Binvert(multiplexer_1_out),
    .Salida(Salida[15]), .Selector(Select), .Carry_out(alu1bits_16_carry_out));
  Alu1bits alu1bits_17 (
    .Carry_int(alu1bits_16_carry_out), .A(A[16]), .B(B[16]), .SLT(1'b0), .Binvert(multiplexer_1_out),
    .Salida(Salida[16]), .Selector(Select), .Carry_out(alu1bits_17_carry_out));
  Alu1bits alu1bits_18 (
    .Carry_int(alu1bits_17_carry_out), .A(A[17]), .B(B[17]), .SLT(1'b0), .Binvert(multiplexer_1_out),
    .Salida(Salida[17]), .Selector(Select), .Carry_out(alu1bits_18_carry_out));
  Alu1bits alu1bits_19 (
    .Carry_int(alu1bits_18_carry_out), .A(A[18]), .B(B[18]), .SLT(1'b0), .Binvert(multiplexer_1_out),
    .Salida(Salida[18]), .Selector(Select), .Carry_out(alu1bits_19_carry_out));
  Alu1bits alu1bits_20 (
    .Carry_int(alu1bits_19_carry_out), .A(A[19]), .B(B[19]), .SLT(1'b0), .Binvert(multiplexer_1_out),
    .Salida(Salida[19]), .Selector(Select), .Carry_out(alu1bits_20_carry_out));
  Alu1bits alu1bits_21 (
    .Carry_int(alu1bits_20_carry_out), .A(A[20]), .B(B[20]), .SLT(1'b0), .Binvert(multiplexer_1_out),
    .Salida(Salida[20]), .Selector(Select), .Carry_out(alu1bits_21_carry_out));
  Alu1bits alu1bits_22 (
    .Carry_int(alu1bits_21_carry_out), .A(A[21]), .B(B[21]), .SLT(1'b0), .Binvert(multiplexer_1_out),
    .Salida(Salida[21]), .Selector(Select), .Carry_out(alu1bits_22_carry_out));
  Alu1bits alu1bits_23 (
    .Carry_int(alu1bits_22_carry_out), .A(A[22]), .B(B[22]), .SLT(1'b0), .Binvert(multiplexer_1_out),
    .Salida(Salida[22]), .Selector(Select), .Carry_out(alu1bits_23_carry_out));
  Alu1bits alu1bits_24 (
    .Carry_int(alu1bits_23_carry_out), .A(A[23]), .B(B[23]), .SLT(1'b0), .Binvert(multiplexer_1_out),
    .Salida(Salida[23]), .Selector(Select), .Carry_out(alu1bits_24_carry_out));
  Alu1bits alu1bits_25 (
    .Carry_int(alu1bits_24_carry_out), .A(A[24]), .B(B[24]), .SLT(1'b0), .Binvert(multiplexer_1_out),
    .Salida(Salida[24]), .Selector(Select), .Carry_out(alu1bits_25_carry_out));
  Alu1bits alu1bits_26 (
    .Carry_int(alu1bits_25_carry_out), .A(A[25]), .B(B[25]), .SLT(1'b0), .Binvert(multiplexer_1_out),
    .Salida(Salida[25]), .Selector(Select), .Carry_out(alu1bits_26_carry_out));
  Alu1bits alu1bits_27 (
    .Carry_int(alu1bits_26_carry_out), .A(A[26]), .B(B[26]), .SLT(1'b0), .Binvert(multiplexer_1_out),
    .Salida(Salida[26]), .Selector(Select), .Carry_out(alu1bits_27_carry_out));
  Alu1bits alu1bits_28 (
    .Carry_int(alu1bits_27_carry_out), .A(A[27]), .B(B[27]), .SLT(1'b0), .Binvert(multiplexer_1_out),
    .Salida(Salida[27]), .Selector(Select), .Carry_out(alu1bits_28_carry_out));
  Alu1bits alu1bits_29 (
    .Carry_int(alu1bits_28_carry_out), .A(A[28]), .B(B[28]), .SLT(1'b0), .Binvert(multiplexer_1_out),
    .Salida(Salida[28]), .Selector(Select), .Carry_out(alu1bits_29_carry_out));
  Alu1bits alu1bits_30 (
    .Carry_int(alu1bits_29_carry_out), .A(A[29]), .B(B[29]), .SLT(1'b0), .Binvert(multiplexer_1_out),
    .Salida(Salida[29]), .Selector(Select), .Carry_out(alu1bits_30_carry_out));
  Alu1bits alu1bits_31 (
    .Carry_int(alu1bits_30_carry_out), .A(A[30]), .B(B[30]), .SLT(1'b0), .Binvert(multiplexer_1_out),
    .Salida(Salida[30]), .Selector(Select), .Carry_out(alu1bits_31_carry_out));
  Alu1bitsOverFlow alu1bitsoverflow_1 (
    .Carry_int(alu1bits_31_carry_out), .A(A[31]), .B(B[31]), .SLT(1'b0), .Binvert(multiplexer_1_out),
    .Salida(Salida[31]), .Selector(Select), .signo(alu1bitsoverflow_1_signo), .overflow(Overflow));  // open: Carry_out
  Multiplexer #(.select(3), .enable("false")) multiplexer_1 (
    .in0(1'b1), .in1(1'b0), .in2(1'b1), .in3(1'b0), .in4(1'b0), .in5(1'b0), .in6(1'b0), .in7(1'b0),
    .out(multiplexer_1_out), .sel(Select));
  or or_1 (or_1_out, Salida[0], Salida[1], Salida[2], Salida[3], Salida[4], Salida[5], Salida[6], Salida[7], Salida[8], Salida[9], Salida[10], Salida[11], Salida[12], Salida[13], Salida[14], Salida[15], Salida[16], Salida[17], Salida[18], Salida[19], Salida[20], Salida[21], Salida[22], Salida[23], Salida[24], Salida[25], Salida[26], Salida[27], Salida[28], Salida[29], Salida[30], Salida[31]);
  not not_1 (zero, or_1_out);
endmodule

module AluControl (
  input  [1:0] in_1,
  input  [5:0] in_2,
  output [2:0] x,
  output J
);

  wire and_2_out, and_3_out, and_4_out, and_5_out, not_1_out, not_2_out, not_3_out, not_4_out, not_5_out,
       not_6_out, not_7_out, not_8_out, not_9_out, not_10_out;

  and and_1 (x[2], in_1[1], in_2[2]);
  and and_2 (and_2_out, in_1[1], in_2[0]);
  and and_3 (and_3_out, in_1[1], in_2[3]);
  not not_1 (not_1_out, in_1[1]);
  not not_2 (not_2_out, in_1[0]);
  not not_3 (not_3_out, in_1[0]);
  not not_4 (not_4_out, in_2[2]);
  not not_5 (not_5_out, in_2[1]);
  not not_6 (not_6_out, in_1[1]);
  not not_7 (not_7_out, in_1[0]);
  not not_8 (not_8_out, in_2[2]);
  not not_9 (not_9_out, in_2[1]);
  not not_10 (not_10_out, in_2[0]);
  or or_1 (x[1], and_2_out, and_3_out);
  and and_4 (and_4_out, not_1_out, not_2_out);
  and and_5 (and_5_out, not_3_out, not_4_out, not_5_out);
  and and_6 (J, not_6_out, not_7_out, in_2[3], not_8_out, not_9_out, not_10_out);
  or or_2 (x[0], and_4_out, and_5_out);
endmodule
