// Logisim project AluControl.circ as structural Verilog
module AluControl (
  input  [1:0] in_1,
  input  [5:0] in_2,
  output [2:0] x,
  output j
);

  wire and_2_out, and_3_out, and_4_out, and_5_out, and_6_out, not_1_out, not_2_out, not_3_out, not_4_out,
       not_5_out, not_6_out, not_7_out, not_8_out, not_9_out, not_10_out, not_11_out;

  and and_1 (x[2], in_1[1], in_2[2]);
  not not_1 (not_1_out, in_2[1]);
  not not_2 (not_2_out, in_1[1]);
  not not_3 (not_3_out, in_1[0]);
  not not_4 (not_4_out, in_1[0]);
  not not_5 (not_5_out, in_2[2]);
  not not_6 (not_6_out, in_2[1]);
  not not_7 (not_7_out, in_1[0]);
  not not_8 (not_8_out, in_1[0]);
  not not_9 (not_9_out, in_2[2]);
  not not_10 (not_10_out, in_2[1]);
  not not_11 (not_11_out, in_2[0]);
  and and_2 (and_2_out, in_1[1], not_1_out, in_2[0]);
  and and_3 (and_3_out, in_1[1], in_2[3]);
  and and_4 (and_4_out, not_2_out, not_3_out);
  and and_5 (and_5_out, not_4_out, not_5_out, not_6_out);
  and and_6 (and_6_out, not_7_out, in_2[2], in_2[1]);
  and and_7 (j, not_8_out, in_2[3], not_9_out, not_10_out, not_11_out);
  or or_1 (x[1], and_2_out, and_3_out);
  or or_2 (x[0], and_4_out, and_5_out, and_6_out);
endmodule
