// Logisim project Lab, Version prueba.circ as structural Verilog: 16 circuits, main circuit main
// 2
module main (
  input  pause,
  input  Reset
);

  wire _0, _1, _2, _3, _4, _5, _6, A, and_1_out, and_2_out, clk, clock_1_out, clock_2_out, colision_1_out_3,
       cpu_1_clear, cpu_1_vida, en, gamenotover, nor_1_out, not_1_out, not_2_out, not_3_out, not_4_out,
       or_1_out, or_2_out, posicionadorfsm_1_out_5, posicionadorfsm_1_out_6, posicionadorfsm_1_out_7,
       posicionadorfsm_1_out_8, posicionadorfsm_1_out_9, S0, S1;
  wire [1:0] STICK;
  wire [5:0] contador6bit_1_out_4;
  wire [31:0] C, display_1_out_5, display_1_out_6, display_1_out_7, display_1_out_8, display_1_out_9,
       display_1_out_10, display_1_out_11, display_1_out_12, display_1_out_13, display_1_out_14,
       display_1_out_15, display_1_out_16, display_1_out_17, display_1_out_18, display_1_out_19,
       display_1_out_20, display_1_out_21, display_1_out_22, display_1_out_23, display_1_out_24,
       display_1_out_25, display_1_out_26, display_1_out_27, display_1_out_28, display_1_out_29,
       display_1_out_30, display_1_out_31, display_1_out_32, display_1_out_33, display_1_out_34,
       display_1_out_35, display_1_out_36, registrodemovimientonav_1_out_8, registrodemovimientonav_1_out_10,
       rom_1_data;

  nand nand_1 (gamenotover, not_1_out, not_2_out, not_3_out, contador6bit_1_out_4[0], contador6bit_1_out_4[3], A, S1, S0);
  not not_1 (not_1_out, contador6bit_1_out_4[5]);
  not not_2 (not_2_out, contador6bit_1_out_4[4]);
  not not_3 (not_3_out, contador6bit_1_out_4[2]);
  contador6bit contador6bit_1 (
    .a(en), .CLOCK(and_1_out), .RESET(or_1_out), .out_4(contador6bit_1_out_4[0]), .out_5(A),
    .out_6(contador6bit_1_out_4[2]), .out_7(contador6bit_1_out_4[3]), .out_8(contador6bit_1_out_4[4]),
    .out_9(contador6bit_1_out_4[5]));
  and and_1 (and_1_out, gamenotover, clk);
  or or_1 (or_1_out, Reset, not_4_out);
  not not_4 (not_4_out, en);
  ROM #(.dataWidth(32)) rom_1 (
    .addr({S0, S1, contador6bit_1_out_4[5:2], A, contador6bit_1_out_4[0]}), .data(rom_1_data), .sel(en));
  and and_2 (and_2_out, clk, gamenotover);
  Clock clock_1 (.out(clock_1_out));
  and and_3 (clk, clock_2_out, nor_1_out);
  Clock #(.highDuration(4), .lowDuration(4)) clock_2 (.out(clock_2_out));
  nor nor_1 (nor_1_out, pause, Reset);
  RegistroDemovimientoNav registrodemovimientonav_1 (
    .E4(posicionadorfsm_1_out_9), .E3(posicionadorfsm_1_out_8), .E2(posicionadorfsm_1_out_7),
    .E1(posicionadorfsm_1_out_6), .E0(posicionadorfsm_1_out_5), .out_8(registrodemovimientonav_1_out_8),
    .out_10(registrodemovimientonav_1_out_10), .in_7(display_1_out_35), .in_1(display_1_out_36), .out_9(C));
  PosicionadorFSM posicionadorfsm_1 (
    .in_R_11(STICK[0]), .in_L_10(STICK[1]), .CLOCK(clock_1_out), .RESET(Reset),
    .out_5(posicionadorfsm_1_out_5), .out_6(posicionadorfsm_1_out_6), .out_7(posicionadorfsm_1_out_7),
    .out_8(posicionadorfsm_1_out_8), .out_9(posicionadorfsm_1_out_9));
  or or_2 (or_2_out, Reset, cpu_1_clear);
  DotMatrix #(.inputtype("row"), .matrixcols(32), .matrixrows(32)) dotmatrix_1 (
    .row0(display_1_out_5), .row1(display_1_out_6), .row2(display_1_out_7), .row3(display_1_out_8),
    .row4(display_1_out_9), .row5(display_1_out_10), .row6(display_1_out_11), .row7(display_1_out_12),
    .row8(display_1_out_13), .row9(display_1_out_14), .row10(display_1_out_15), .row11(display_1_out_16),
    .row12(display_1_out_17), .row13(display_1_out_18), .row14(display_1_out_19), .row15(display_1_out_20),
    .row16(display_1_out_21), .row17(display_1_out_22), .row18(display_1_out_23), .row19(display_1_out_24),
    .row20(display_1_out_25), .row21(display_1_out_26), .row22(display_1_out_27), .row23(display_1_out_28),
    .row24(display_1_out_29), .row25(display_1_out_30), .row26(display_1_out_31), .row27(display_1_out_32),
    .row28(display_1_out_33), .row29(display_1_out_34), .row30(registrodemovimientonav_1_out_10),
    .row31(registrodemovimientonav_1_out_8));
  display display_1 (
    .in_1(rom_1_data), .in_2(en), .in_3(and_2_out), .in_4(or_2_out), .out_5(display_1_out_5),
    .out_6(display_1_out_6), .out_7(display_1_out_7), .out_8(display_1_out_8), .out_9(display_1_out_9),
    .out_10(display_1_out_10), .out_11(display_1_out_11), .out_12(display_1_out_12),
    .out_13(display_1_out_13), .out_14(display_1_out_14), .out_15(display_1_out_15),
    .out_16(display_1_out_16), .out_17(display_1_out_17), .out_18(display_1_out_18),
    .out_19(display_1_out_19), .out_20(display_1_out_20), .out_21(display_1_out_21),
    .out_22(display_1_out_22), .out_23(display_1_out_23), .out_24(display_1_out_24),
    .out_25(display_1_out_25), .out_26(display_1_out_26), .out_27(display_1_out_27),
    .out_28(display_1_out_28), .out_29(display_1_out_29), .out_30(display_1_out_30),
    .out_31(display_1_out_31), .out_32(display_1_out_32), .out_33(display_1_out_33),
    .out_34(display_1_out_34), .out_35(display_1_out_35), .out_36(display_1_out_36));
  colision colision_1 (.in_1(display_1_out_34), .in_2(C), .out_3(colision_1_out_3));
  CPU cpu_1 (.in_1(colision_1_out_3), .in_2(1'b0), .in_3(clk), .enable(en), .clear(cpu_1_clear), .vida(cpu_1_vida));
  Vida vida_1 (
    .Reloj(clk), .Entrada(cpu_1_vida), .Reset(Reset), .out_4(_0), .out_5(_1), .out_6(_2), .out_7(_3),
    .out_8(_4), .out_9(_5), .out_10(_6), .out_11(S0), .out_12(S1));
  _7_Segment_Display u_7_segment_display_1 (.g(_6), .f(_5), .a(_0), .b(_1), .e(_4), .d(_3), .c(_2));  // open: dp
  Joystick #(.bits(2)) joystick_1 (.x(STICK));  // open: y

  // Notes on the sheet:
  //   ENABLE
  //   contents of rom_1 (hex, n*v repeats v):
  //   4000001 4000001 200 1208 601008 0 600000 c0600000 c000e000 e000 c c 180 7000180 7000000 0 e0000
  //   e0000 c0000010 c0000010 c00 200c00 200003 3 0 0 0 c000000 20000 200e0 e0 0 4000001 4000001 200 1208
  //   601008 0 600000 c0600000 c000e000 e000 c c 180 7000180 7000000 0 e0000 e0000 c0000010 c0000010 c00
  //   200c00 200003 3 0 0 0 c000000 20000 200e0 e0 0 4000001 e000003 4040201 e1708 43a1c 1008 400000
  //   40e00000 e0404000 e000 4004 e 104 2000380 7000100 2000000 40000 e0000 40040010 e0000038 40000410
  //   200e00 700402 200007 2 0 0 8000000 1c020000 8070040 200e0 40 4000001 e000003 4040201 e1708 43a1c
  //   1008 400000 40e00000 e0404000 e000 4004 e 104 2000380 7000100 2000000 40000 e0000 40040010 e0000038
  //   40000410 200e00 700402 200007 2 0 0 8000000 1c020000 8070040 200e0 40 f8000000 70000000 200007c0
  //   f8380 70100 20000 0 1f000000 e00001f 400000e 1f004 e000 4000 0 f80000 7007c0 200380 100 0 7c000000
  //   3803e000 1001c07c 8038 10 1f00000 e00000 403e00 1c00 81f e 4 0 f8000000 70000000 200007c0 f8380
  //   70100 20000 0 1f000000 e00001f 400000e 1f004 e000 4000 0 f80000 7007c0 200380 100 0 7c000000
  //   3803e000 1c07c c038 10 1f00000 e00000 403e00 1c00 81f e 4 0 3c9d400 2551800 2559800 2551400 3d5d800
  //   0 3d51780 25d1400 2dd5700 215b400 3dd1780
  //   CPU
endmodule

module adder (
  input  in_1,
  input  A,
  input  b,
  input  A_2,
  input  b_2,
  input  A_3,
  input  b_3,
  input  A_4,
  input  b_4,
  input  A_5,
  input  b_5,
  output out_12,
  output out_13,
  output out_14,
  output out_15,
  output out_16,
  output msb
);

  wire adder_1_cout, adder_2_cout, adder_3_cout, adder_4_cout, xor_1_out, xor_2_out, xor_3_out, xor_4_out,
       xor_5_out;

  xor xor_1 (xor_1_out, b, in_1);
  xor xor_2 (xor_2_out, b_2, in_1);
  xor xor_3 (xor_3_out, b_3, in_1);
  xor xor_4 (xor_4_out, b_4, in_1);
  xor xor_5 (xor_5_out, b_5, in_1);
  Adder #(.width(1)) adder_1 (.a(A), .b(xor_1_out), .out(out_12), .cin(in_1), .cout(adder_1_cout));
  Adder #(.width(1)) adder_2 (.a(A_2), .b(xor_2_out), .out(out_13), .cin(adder_1_cout), .cout(adder_2_cout));
  Adder #(.width(1)) adder_3 (.a(A_3), .b(xor_3_out), .out(out_14), .cin(adder_2_cout), .cout(adder_3_cout));
  Adder #(.width(1)) adder_4 (.a(A_4), .b(xor_4_out), .out(out_15), .cin(adder_3_cout), .cout(adder_4_cout));
  Adder #(.width(1)) adder_5 (.a(A_5), .b(xor_5_out), .out(out_16), .cin(adder_4_cout), .cout(msb));
endmodule

module Posicionador (
  input  P,
  input  B,
  input  CLOCK,
  input  RESET,
  output out_5,
  output out_6,
  output out_7,
  output out_8,
  output out_9
);

  wire adder_1_out_12, adder_1_out_13, adder_1_out_14, adder_1_out_15, adder_1_out_16, and_1_out, and_2_out,
       and_3_out, and_4_out, and_5_out, and_6_out, and_7_out, and_8_out, not_1_out, not_2_out, not_3_out,
       not_4_out, not_5_out, not_6_out, not_7_out, not_8_out, not_9_out, not_10_out, not_11_out, not_12_out,
       not_13_out, not_14_out, or_1_out;

  and and_1 (and_1_out, P, B, not_1_out, not_3_out, not_2_out, not_4_out, not_5_out);
  not not_1 (not_1_out, out_5);
  not not_2 (not_2_out, out_7);
  not not_3 (not_3_out, out_6);
  not not_4 (not_4_out, out_8);
  not not_5 (not_5_out, out_9);
  not not_6 (not_6_out, P);
  not not_7 (not_7_out, out_6);
  not not_8 (not_8_out, and_1_out);
  adder adder_1 (
    .in_1(P), .A(out_5), .b(B), .A_2(out_6), .b_2(1'b0), .A_3(out_7), .b_3(1'b0), .A_4(out_8), .b_4(1'b0),
    .A_5(out_9), .b_5(1'b0), .out_12(adder_1_out_12), .out_13(adder_1_out_13), .out_14(adder_1_out_14),
    .out_15(adder_1_out_15), .out_16(adder_1_out_16));  // open: msb
  and and_2 (and_2_out, not_6_out, out_5, not_7_out, out_7, out_9, out_8, B);
  and and_3 (and_3_out, not_8_out, or_1_out);
  or or_1 (or_1_out, adder_1_out_12, and_2_out);
  and and_4 (and_4_out, not_8_out, adder_1_out_13);
  and and_5 (and_5_out, not_8_out, adder_1_out_14);
  not not_9 (not_9_out, and_2_out);
  not not_10 (not_10_out, and_3_out);
  not not_11 (not_11_out, and_6_out);
  and and_6 (and_6_out, and_4_out, not_9_out);
  not not_12 (not_12_out, and_5_out);
  and and_7 (and_7_out, not_8_out, adder_1_out_15);
  not not_13 (not_13_out, and_7_out);
  and and_8 (and_8_out, not_8_out, adder_1_out_16);
  not not_14 (not_14_out, and_8_out);
  S_R_Flip_Flop s_r_ff_1 (
    .S(and_3_out), .clk(CLOCK), .R(not_10_out), .Q(out_5), .preset(RESET), .en(CLOCK));  // open: Qn, reset
  S_R_Flip_Flop s_r_ff_2 (
    .S(and_6_out), .clk(CLOCK), .R(not_11_out), .Q(out_6), .preset(RESET), .en(CLOCK));  // open: Qn, reset
  S_R_Flip_Flop s_r_ff_3 (
    .S(and_5_out), .clk(CLOCK), .R(not_12_out), .Q(out_7), .preset(RESET), .en(CLOCK));  // open: Qn, reset
  S_R_Flip_Flop s_r_ff_4 (
    .S(and_7_out), .clk(CLOCK), .R(not_13_out), .Q(out_8), .preset(RESET), .en(CLOCK));  // open: Qn, reset
  S_R_Flip_Flop s_r_ff_5 (
    .S(and_8_out), .clk(CLOCK), .R(not_14_out), .Q(out_9), .reset(RESET), .en(CLOCK));  // open: Qn, preset

  // Other names for the same wires on the sheet: _0 = out_5; _1 = out_6; _2 = out_7; _3 = out_8; _4 = out_9

  // Notes on the sheet:
  //   a
  //   a
  //   b
  //   a
  //   b
  //   a
  //   b
  //   a
  //   b
  //   MSB
  //   MSB
endmodule

module playerGui (
  input  in_1,
  input  in_2,
  input  in_3,
  input  in_4,
  input  in_5,
  output [31:0] out_6,
  output [31:0] out_7
);

  Shifter #(.width(32)) shifter_1 (.in(32'h2), .\dist ({in_1, in_2, in_3, in_4, in_5}), .out(out_6));
  Shifter #(.width(32)) shifter_2 (.in(32'h5), .\dist ({in_1, in_2, in_3, in_4, in_5}), .out(out_7));
endmodule

module adder6bit (
  input  in_1,
  input  A,
  input  b,
  input  A_2,
  input  b_2,
  input  A_3,
  input  b_3,
  input  A_4,
  input  b_4,
  input  A_5,
  input  b_5,
  input  A_6,
  input  b_6,
  output out_14,
  output out_15,
  output out_16,
  output out_17,
  output out_18,
  output out_19,
  output msb
);

  wire adder_1_cout, adder_2_cout, adder_3_cout, adder_4_cout, adder_5_cout, xor_1_out, xor_2_out, xor_3_out,
       xor_4_out, xor_5_out, xor_6_out;

  xor xor_1 (xor_1_out, b, in_1);
  xor xor_2 (xor_2_out, b_2, in_1);
  xor xor_3 (xor_3_out, b_3, in_1);
  xor xor_4 (xor_4_out, b_4, in_1);
  xor xor_5 (xor_5_out, b_5, in_1);
  xor xor_6 (xor_6_out, b_6, in_1);
  Adder #(.width(1)) adder_1 (.a(A), .b(xor_1_out), .out(out_14), .cin(in_1), .cout(adder_1_cout));
  Adder #(.width(1)) adder_2 (.a(A_2), .b(xor_2_out), .out(out_15), .cin(adder_1_cout), .cout(adder_2_cout));
  Adder #(.width(1)) adder_3 (.a(A_3), .b(xor_3_out), .out(out_16), .cin(adder_2_cout), .cout(adder_3_cout));
  Adder #(.width(1)) adder_4 (.a(A_4), .b(xor_4_out), .out(out_17), .cin(adder_3_cout), .cout(adder_4_cout));
  Adder #(.width(1)) adder_5 (.a(A_5), .b(xor_5_out), .out(out_18), .cin(adder_4_cout), .cout(adder_5_cout));
  Adder #(.width(1)) adder_6 (.a(A_6), .b(xor_6_out), .out(out_19), .cin(adder_5_cout), .cout(msb));
endmodule

module PosicionadorFSM (
  input  in_R_11,
  input  in_L_10,
  input  CLOCK,
  input  RESET,
  output out_5,
  output out_6,
  output out_7,
  output out_8,
  output out_9
);

  wire _0_prime, _1_prime, _2_prime, _3_prime, _4_prime, and_1_out, and_2_out, and_3_out, and_4_out,
       and_5_out, and_6_out, and_7_out, and_8_out, and_9_out, and_10_out, and_11_out, and_12_out, and_13_out,
       and_14_out, and_15_out, and_16_out, and_17_out, and_18_out, and_19_out, and_20_out, and_21_out,
       and_22_out, and_23_out, and_24_out, and_25_out, and_26_out, and_27_out, and_28_out, and_29_out,
       and_30_out, and_31_out, and_33_out, and_34_out, and_35_out, and_37_out, and_38_out, L, not_5_out,
       not_6_out, not_8_out, not_9_out, not_10_out, or_1_out, or_2_out, or_3_out, or_4_out, or_5_out,
       or_6_out, or_7_out, or_8_out, or_9_out, or_10_out, or_11_out, or_12_out, R, R0, R1, R2, R3, S1, S2,
       undriven;

  not not_1 (_4_prime, out_9);
  not not_2 (_2_prime, out_7);
  not not_3 (_3_prime, out_8);
  not not_4 (_1_prime, out_6);
  not not_5 (not_5_out, in_R_11);
  not not_6 (not_6_out, in_L_10);
  not not_7 (_0_prime, out_5);
  and and_1 (and_1_out, _0_prime, _1_prime, _2_prime, out_9, _3_prime, R);
  not not_8 (not_8_out, _3_prime);
  and and_2 (and_2_out, _3_prime, _1_prime, _2_prime, R, _0_prime);
  and _11_R (R, in_L_10, in_R_11);
  and and_3 (and_3_out, R, out_5, _1_prime, out_7, out_8);
  and and_4 (and_4_out, R, out_5, _3_prime);
  and and_5 (and_5_out, R, _4_prime, out_5);
  and and_6 (and_6_out, R, _0_prime, out_6, _3_prime);
  and and_7 (and_7_out, _0_prime, _2_prime, out_9, R);
  and and_8 (and_8_out, R, _0_prime, out_6, _4_prime);
  and and_9 (and_9_out, R, _0_prime, _1_prime, out_8);
  and and_10 (and_10_out, R, _0_prime, _1_prime, out_7);
  and and_11 (and_11_out, R, _0_prime, out_6, _3_prime);
  and and_12 (and_12_out, R, _0_prime, out_6, _2_prime, out_8);
  or or_1 (or_1_out, and_11_out, and_12_out, and_13_out);
  and and_13 (and_13_out, R, _0_prime, out_6, _4_prime);
  and and_14 (and_14_out, R, _0_prime, _1_prime, out_9);
  and and_15 (and_15_out, R, _0_prime, _1_prime, out_7);
  or or_2 (or_2_out, and_14_out, and_15_out, and_16_out);
  and and_16 (and_16_out, R, _0_prime, _1_prime, out_8);
  and and_17 (and_17_out, _0_prime, _1_prime, _2_prime, out_9, R);
  and and_18 (and_18_out, _0_prime, _2_prime, not_8_out, _1_prime, R);
  and _10_L (L, in_R_11, not_6_out);
  and and_19 (and_19_out, out_5, out_8, R, _2_prime);
  or or_3 (or_3_out, and_3_out, and_19_out, and_4_out, and_5_out);
  or or_4 (or_4_out, and_6_out, and_7_out, and_10_out, and_8_out, and_9_out);
  and and_20 (and_20_out, _0_prime, L);
  or or_5 (or_5_out, and_17_out, S2, and_21_out);
  and and_21 (and_21_out, _0_prime, _1_prime, _2_prime, out_8, R);
  or or_6 (or_6_out, and_18_out, R3);
  not not_9 (not_9_out, _3_prime);
  or or_7 (or_7_out, or_4_out, and_20_out);
  or or_8 (or_8_out, or_3_out, R0);
  or or_9 (or_9_out, S1, or_2_out);
  or or_10 (or_10_out, or_1_out, R1);
  and and_22 (and_22_out, _0_prime, _1_prime, out_7, R);
  and and_23 (and_23_out, _3_prime, out_7, out_6, out_5, L);
  and and_24 (and_24_out, out_5, out_6, out_7, _4_prime, L, out_8);
  and and_25 (and_25_out, L, not_9_out, out_5, _2_prime);
  and and_26 (and_26_out, out_6, out_5, L);
  and and_27 (and_27_out, L, out_5, _3_prime);
  and and_28 (and_28_out, L, _4_prime, out_5);
  and and_29 (and_29_out, _2_prime, out_6, out_8, out_5, L);
  and and_30 (and_30_out, _4_prime, out_6, out_5, L);
  and and_31 (and_31_out, _3_prime, L, out_6, out_5);
  S_R_Flip_Flop s_r_ff_1 (
    .S(or_7_out), .clk(CLOCK), .R(or_8_out), .Q(out_5), .preset(RESET), .en(CLOCK));  // open: Qn, reset
  S_R_Flip_Flop s_r_ff_2 (
    .S(or_9_out), .clk(CLOCK), .R(or_10_out), .Q(out_6), .preset(RESET), .en(CLOCK));  // open: Qn, reset
  S_R_Flip_Flop s_r_ff_3 (
    .S(or_5_out), .clk(CLOCK), .R(or_11_out), .Q(out_7), .preset(RESET), .en(CLOCK));  // open: Qn, reset
  or or_11 (or_11_out, and_22_out, R2);
  S_R_Flip_Flop s_r_ff_4 (
    .S(or_12_out), .clk(CLOCK), .R(or_6_out), .Q(out_8), .preset(RESET), .en(CLOCK));  // open: Qn, reset
  or or_12 (or_12_out, and_1_out, and_23_out);
  S_R_Flip_Flop s_r_ff_5 (
    .S(and_24_out), .clk(CLOCK), .R(and_2_out), .Q(out_9), .preset(undriven), .reset(RESET), .en(CLOCK));  // open: Qn
  or or_13 (R0, and_25_out, and_26_out, and_27_out, and_28_out);
  or or_14 (R1, and_29_out, and_30_out, and_31_out);
  not not_10 (not_10_out, out_8);
  and and_32 (R3, _4_prime, out_8, out_7, out_6, out_5, L);
  and and_33 (and_33_out, out_5, _1_prime, not_10_out, L);
  and and_34 (and_34_out, _4_prime, L, _1_prime, out_5);
  or or_15 (S1, and_34_out, and_33_out, and_35_out);
  and and_35 (and_35_out, out_8, _2_prime, L, _1_prime, out_5);
  and and_36 (S2, L, _2_prime, out_6, out_5);
  and and_37 (and_37_out, _4_prime, out_7, L, out_6, out_5);
  or or_16 (R2, and_37_out, and_38_out);
  and and_38 (and_38_out, out_7, out_6, out_5, _3_prime, L);

  // Other names for the same wires on the sheet: _0 = out_5; _1 = out_6; _2 = out_7; _3 = out_8; _4 = out_9

  // Notes on the sheet:
  //   MSB
endmodule

module display (
  input  [31:0] in_1,
  input  in_2,
  input  in_3,
  input  in_4,
  output [31:0] out_5,
  output [31:0] out_6,
  output [31:0] out_7,
  output [31:0] out_8,
  output [31:0] out_9,
  output [31:0] out_10,
  output [31:0] out_11,
  output [31:0] out_12,
  output [31:0] out_13,
  output [31:0] out_14,
  output [31:0] out_15,
  output [31:0] out_16,
  output [31:0] out_17,
  output [31:0] out_18,
  output [31:0] out_19,
  output [31:0] out_20,
  output [31:0] out_21,
  output [31:0] out_22,
  output [31:0] out_23,
  output [31:0] out_24,
  output [31:0] out_25,
  output [31:0] out_26,
  output [31:0] out_27,
  output [31:0] out_28,
  output [31:0] out_29,
  output [31:0] out_30,
  output [31:0] out_31,
  output [31:0] out_32,
  output [31:0] out_33,
  output [31:0] out_34,
  output [31:0] out_35,
  output [31:0] out_36
);

  Register #(.width(32)) register_1 (.D(out_6), .en(in_2), .Q(out_7), .clk(in_3), .clr(in_4));
  Register #(.width(32)) register_2 (.D(in_1), .en(in_2), .Q(out_6), .clk(in_3), .clr(in_4));
  Register #(.width(32)) register_3 (.D(out_21), .en(in_2), .Q(out_22), .clk(in_3), .clr(in_4));
  Register #(.width(32)) register_4 (.D(out_22), .en(in_2), .Q(out_23), .clk(in_3), .clr(in_4));
  Register #(.width(32)) register_5 (.D(out_7), .Q(out_8), .clk(in_3), .clr(in_4));  // open: en
  Register #(.width(32)) register_6 (.D(out_23), .en(in_2), .Q(out_24), .clk(in_3), .clr(in_4));
  Register #(.width(32)) register_7 (.D(out_9), .en(in_2), .Q(out_10), .clk(in_3), .clr(in_4));
  Register #(.width(32)) register_8 (.D(out_8), .en(in_2), .Q(out_9), .clk(in_3), .clr(in_4));
  Register #(.width(32)) register_9 (.D(out_24), .en(in_2), .Q(out_25), .clk(in_3), .clr(in_4));
  Register #(.width(32)) register_10 (.D(out_25), .en(in_2), .Q(out_26), .clk(in_3), .clr(in_4));
  Register #(.width(32)) register_11 (.D(out_10), .en(in_2), .Q(out_11), .clk(in_3), .clr(in_4));
  Register #(.width(32)) register_12 (.D(out_26), .en(in_2), .Q(out_27), .clk(in_3), .clr(in_4));
  Register #(.width(32)) register_13 (.D(out_11), .en(in_2), .Q(out_12), .clk(in_3), .clr(in_4));
  Register #(.width(32)) register_14 (.D(out_12), .en(in_2), .Q(out_13), .clk(in_3), .clr(in_4));
  Register #(.width(32)) register_15 (.D(out_27), .en(in_2), .Q(out_28), .clk(in_3), .clr(in_4));
  Register #(.width(32)) register_16 (.D(out_28), .en(in_2), .Q(out_29), .clk(in_3), .clr(in_4));
  Register #(.width(32)) register_17 (.D(out_14), .en(in_2), .Q(out_15), .clk(in_3), .clr(in_4));
  Register #(.width(32)) register_18 (.D(out_13), .en(in_2), .Q(out_14), .clk(in_3), .clr(in_4));
  Register #(.width(32)) register_19 (.D(out_30), .en(in_2), .Q(out_31), .clk(in_3), .clr(in_4));
  Register #(.width(32)) register_20 (.D(out_29), .en(in_2), .Q(out_30), .clk(in_3), .clr(in_4));
  Register #(.width(32)) register_21 (.D(out_15), .en(in_2), .Q(out_16), .clk(in_3), .clr(in_4));
  Register #(.width(32)) register_22 (.D(out_31), .en(in_2), .Q(out_32), .clk(in_3), .clr(in_4));
  Register #(.width(32)) register_23 (.D(out_17), .en(in_2), .Q(out_18), .clk(in_3), .clr(in_4));
  Register #(.width(32)) register_24 (.D(out_16), .en(in_2), .Q(out_17), .clk(in_3), .clr(in_4));
  Register #(.width(32)) register_25 (.D(out_32), .en(in_2), .Q(out_33), .clk(in_3), .clr(in_4));
  Register #(.width(32)) register_26 (.D(out_33), .en(in_2), .Q(out_34), .clk(in_3), .clr(in_4));
  Register #(.width(32)) register_27 (.D(out_18), .en(in_2), .Q(out_19), .clk(in_3), .clr(in_4));
  Register #(.width(32)) register_28 (.D(out_34), .en(in_2), .Q(out_35), .clk(in_3), .clr(in_4));
  Register #(.width(32)) register_29 (.D(out_20), .en(in_2), .Q(out_21), .clk(in_3), .clr(in_4));
  Register #(.width(32)) register_30 (.D(out_19), .en(in_2), .Q(out_20), .clk(in_3), .clr(in_4));
  Register #(.width(32)) register_31 (.D(out_36), .en(in_2), .clk(in_3), .clr(in_4));  // open: Q
  Register #(.width(32)) register_32 (.D(out_35), .en(in_2), .Q(out_36), .clk(in_3), .clr(in_4));

  assign out_5 = in_1;

  // Other names for the same wires on the sheet: _0[31:0] = in_1; _1[31:0] = out_6; _2[31:0] = out_7;
  //   _3[31:0] = out_8; _4[31:0] = out_9; _5[31:0] = out_10; _6[31:0] = out_11; _7[31:0] = out_12; _8[31:0] = out_13;
  //   _9[31:0] = out_14; _10[31:0] = out_15; _11[31:0] = out_16; _12[31:0] = out_17; _13[31:0] = out_18;
  //   _14[31:0] = out_19; _15[31:0] = out_20; _16[31:0] = out_21; _17[31:0] = out_22; _18[31:0] = out_23;
  //   _19[31:0] = out_24; _20[31:0] = out_25; _21[31:0] = out_26; _22[31:0] = out_27; _23[31:0] = out_28;
  //   _24[31:0] = out_29; _25[31:0] = out_30; _26[31:0] = out_31; _27[31:0] = out_32; _28[31:0] = out_33;
  //   _29[31:0] = out_34; _30[31:0] = out_35; _31[31:0] = out_36; clk = in_3; clr = in_4; en = in_2

  // Notes on the sheet:
  //   D in
endmodule

module contador6bit (
  input  a,
  input  CLOCK,
  input  RESET,
  output out_4,
  output out_5,
  output out_6,
  output out_7,
  output out_8,
  output out_9
);

  wire adder6bit_1_out_14, adder6bit_1_out_15, adder6bit_1_out_16, adder6bit_1_out_17, adder6bit_1_out_18,
       adder6bit_1_out_19, not_1_out, not_2_out, not_3_out, not_4_out, not_5_out, not_6_out;

  adder6bit adder6bit_1 (
    .in_1(1'b0), .A(out_4), .b(a), .A_2(out_5), .b_2(1'b0), .A_3(out_6), .b_3(1'b0), .A_4(out_7), .b_4(1'b0),
    .A_5(out_8), .b_5(1'b0), .A_6(out_9), .b_6(1'b0), .out_14(adder6bit_1_out_14),
    .out_15(adder6bit_1_out_15), .out_16(adder6bit_1_out_16), .out_17(adder6bit_1_out_17),
    .out_18(adder6bit_1_out_18), .out_19(adder6bit_1_out_19));  // open: msb
  not not_1 (not_1_out, adder6bit_1_out_14);
  not not_2 (not_2_out, adder6bit_1_out_15);
  not not_3 (not_3_out, adder6bit_1_out_16);
  not not_4 (not_4_out, adder6bit_1_out_17);
  not not_5 (not_5_out, adder6bit_1_out_18);
  not not_6 (not_6_out, adder6bit_1_out_19);
  S_R_Flip_Flop s_r_ff_1 (
    .S(adder6bit_1_out_14), .clk(CLOCK), .R(not_1_out), .Q(out_4), .reset(RESET), .en(CLOCK));  // open: Qn, preset
  S_R_Flip_Flop s_r_ff_2 (
    .S(adder6bit_1_out_15), .clk(CLOCK), .R(not_2_out), .Q(out_5), .reset(RESET), .en(CLOCK));  // open: Qn, preset
  S_R_Flip_Flop s_r_ff_3 (
    .S(adder6bit_1_out_16), .clk(CLOCK), .R(not_3_out), .Q(out_6), .reset(RESET), .en(CLOCK));  // open: Qn, preset
  S_R_Flip_Flop s_r_ff_4 (
    .S(adder6bit_1_out_17), .clk(CLOCK), .R(not_4_out), .Q(out_7), .reset(RESET), .en(CLOCK));  // open: Qn, preset
  S_R_Flip_Flop s_r_ff_5 (
    .S(adder6bit_1_out_18), .clk(CLOCK), .R(not_5_out), .Q(out_8), .reset(RESET), .en(CLOCK));  // open: Qn, preset
  S_R_Flip_Flop s_r_ff_6 (
    .S(adder6bit_1_out_19), .clk(CLOCK), .R(not_6_out), .Q(out_9), .reset(RESET), .en(CLOCK));  // open: Qn, preset

  // Other names for the same wires on the sheet: _0 = out_4; _1 = out_5; _2 = out_6; _3 = out_7; _4 = out_8;
  //   _5 = out_9

  // Notes on the sheet:
  //   a
  //   b
  //   a
  //   b
  //   a
  //   b
  //   a
  //   b
  //   a
  //   b
  //   MSB
  //   ESCENARIO 6 BIT
endmodule

module RM_Parte_superior (
  input  E0,
  input  E1,
  input  E2,
  input  E3,
  input  E4,
  output out_6,
  output out_7,
  output out_8,
  output out_9,
  output out_10,
  output out_11,
  output out_12,
  output out_13,
  output out_14,
  output out_15,
  output out_16,
  output out_17,
  output out_18,
  output out_19,
  output out_20,
  output out_21,
  output out_22,
  output out_23,
  output out_24,
  output out_25,
  output out_26,
  output out_27,
  output out_28,
  output out_29,
  output out_30,
  output out_31,
  output out_32,
  output out_33,
  output out_34,
  output out_35,
  output out_36,
  output out_37
);

  wire not_1_out, not_2_out, not_3_out, not_4_out, not_5_out;

  not not_1 (not_1_out, E0);
  not not_2 (not_2_out, E1);
  not not_3 (not_3_out, E2);
  not not_4 (not_4_out, E3);
  not not_5 (not_5_out, E4);
  and and_1 (out_6, 1'b0, E0, E1, E2, E3, E4);
  and and_2 (out_7, not_1_out, not_2_out, not_3_out, not_4_out, not_5_out);
  and and_3 (out_8, E0, not_2_out, not_3_out, not_4_out, not_5_out);
  and and_4 (out_9, not_1_out, E1, not_3_out, not_4_out, not_5_out);
  and and_5 (out_10, E0, E1, not_3_out, not_4_out, not_5_out);
  and and_6 (out_11, not_1_out, not_2_out, E2, not_4_out, not_5_out);
  and and_7 (out_12, E0, not_2_out, E2, not_4_out, not_5_out);
  and and_8 (out_13, not_1_out, E1, E2, not_4_out, not_5_out);
  and and_9 (out_14, E0, E1, E2, not_4_out, not_5_out);
  and and_10 (out_15, not_1_out, not_2_out, not_3_out, E3, not_5_out);
  and and_11 (out_16, E0, not_2_out, not_3_out, E3, not_5_out);
  and and_12 (out_17, not_1_out, E1, not_3_out, E3, not_5_out);
  and and_13 (out_18, E0, E1, not_3_out, E3, not_5_out);
  and and_14 (out_19, not_1_out, not_2_out, E2, E3, not_5_out);
  and and_15 (out_20, E0, not_2_out, E2, E3, not_5_out);
  and and_16 (out_21, not_1_out, E1, E2, E3, not_5_out);
  and and_17 (out_22, E0, E1, E2, E3, not_5_out);
  and and_18 (out_23, not_1_out, not_2_out, not_3_out, not_4_out, E4);
  and and_19 (out_24, E0, not_2_out, not_3_out, not_4_out, E4);
  and and_20 (out_25, not_1_out, E1, not_3_out, not_4_out, E4);
  and and_21 (out_26, E0, E1, not_3_out, not_4_out, E4);
  and and_22 (out_27, not_1_out, not_2_out, E2, not_4_out, E4);
  and and_23 (out_28, E0, not_2_out, E2, not_4_out, E4);
  and and_24 (out_29, not_1_out, E1, E2, not_4_out, E4);
  and and_25 (out_30, E0, E1, E2, not_4_out, E4);
  and and_26 (out_31, not_1_out, not_2_out, not_3_out, E3, E4);
  and and_27 (out_32, E0, not_2_out, not_3_out, E3, E4);
  and and_28 (out_33, not_1_out, E1, not_3_out, E3, E4);
  and and_29 (out_34, E0, E1, not_3_out, E3, E4);
  and and_30 (out_35, not_1_out, not_2_out, E2, E3, E4);
  and and_31 (out_36, E0, not_2_out, E2, E3, E4);
  and and_32 (out_37, not_1_out, E1, E2, E3, E4);
endmodule

module RM_Parte_Inferior (
  input  E0,
  input  E1,
  input  E2,
  input  E3,
  input  E4,
  output out_6,
  output s1,
  output s2,
  output s3,
  output s4,
  output s5,
  output s6,
  output s7,
  output s8,
  output s9,
  output s10,
  output s11,
  output s12,
  output s13,
  output s14,
  output s15,
  output S16,
  output S17,
  output S18,
  output S19,
  output s20,
  output s21,
  output s22,
  output s23,
  output s24,
  output s25,
  output s26,
  output S27,
  output S28,
  output S29,
  output S30,
  output S31
);

  wire and_5_out, and_6_out, and_7_out, and_8_out, and_11_out, and_12_out, and_13_out, and_14_out,
       and_17_out, and_18_out, and_19_out, and_20_out, and_23_out, and_24_out, and_25_out, and_26_out,
       and_29_out, and_30_out, and_31_out, and_32_out, and_35_out, and_36_out, and_37_out, and_38_out,
       and_41_out, and_42_out, and_43_out, and_44_out, and_45_out, and_46_out, not_1_out, not_2_out,
       not_3_out, not_4_out, not_5_out;

  not not_1 (not_1_out, E0);
  not not_2 (not_2_out, E1);
  not not_3 (not_3_out, E2);
  not not_4 (not_4_out, E3);
  not not_5 (not_5_out, E4);
  and and_1 (out_6, not_1_out, not_2_out, not_3_out, not_4_out, not_5_out);
  and and_2 (s1, E0, not_2_out, not_3_out, not_4_out, not_5_out);
  and and_3 (s2, not_1_out, not_3_out, not_4_out, not_5_out);
  and and_4 (s3, E0, not_3_out, not_4_out, not_5_out);
  and and_5 (and_5_out, not_1_out, E1, not_3_out, not_4_out, not_5_out);
  and and_6 (and_6_out, not_1_out, not_2_out, E2, not_4_out, not_5_out);
  and and_7 (and_7_out, E0, E1, not_3_out, not_4_out, not_5_out);
  and and_8 (and_8_out, E0, not_2_out, E2, not_4_out, not_5_out);
  and and_9 (s6, not_1_out, E2, not_4_out, not_5_out);
  and and_10 (s7, E0, E2, not_4_out, not_5_out);
  and and_11 (and_11_out, not_1_out, E1, E2, not_4_out, not_5_out);
  and and_12 (and_12_out, not_1_out, not_2_out, not_3_out, E3, not_5_out);
  and and_13 (and_13_out, E0, E1, E2, not_4_out, not_5_out);
  and and_14 (and_14_out, E0, not_2_out, not_3_out, E3, not_5_out);
  and and_15 (s10, not_1_out, not_3_out, E3, not_5_out);
  and and_16 (s11, E0, not_3_out, E3, not_5_out);
  and and_17 (and_17_out, not_1_out, E1, not_3_out, E3, not_5_out);
  and and_18 (and_18_out, not_1_out, not_2_out, E2, E3, not_5_out);
  and and_19 (and_19_out, E0, E1, not_3_out, E3, not_5_out);
  and and_20 (and_20_out, E0, not_2_out, E2, E3, not_5_out);
  and and_21 (s14, not_1_out, E2, E3, not_5_out);
  and and_22 (s15, E0, E2, E3, not_5_out);
  and and_23 (and_23_out, not_1_out, E1, E2, E3, not_5_out);
  and and_24 (and_24_out, not_1_out, not_2_out, not_3_out, not_4_out, E4);
  and and_25 (and_25_out, E0, E1, E2, E3, not_5_out);
  and and_26 (and_26_out, E0, not_2_out, not_3_out, not_4_out, E4);
  and and_27 (S18, not_1_out, not_3_out, not_4_out, E4);
  and and_28 (S19, E0, not_3_out, not_4_out, E4);
  and and_29 (and_29_out, not_1_out, E1, not_3_out, not_4_out, E4);
  and and_30 (and_30_out, not_1_out, not_2_out, E2, not_4_out, E4);
  and and_31 (and_31_out, E0, E1, not_3_out, not_4_out, E4);
  and and_32 (and_32_out, E0, not_2_out, E2, not_4_out, E4);
  and and_33 (s22, not_1_out, E2, not_4_out, E4);
  and and_34 (s23, E0, E2, not_4_out, E4);
  and and_35 (and_35_out, not_1_out, E1, E2, not_4_out, E4);
  and and_36 (and_36_out, not_1_out, not_2_out, not_3_out, E3, E4);
  and and_37 (and_37_out, E0, E1, E2, not_4_out, E4);
  and and_38 (and_38_out, E0, not_2_out, not_3_out, E3, E4);
  and and_39 (s26, not_1_out, not_3_out, E3, E4);
  and and_40 (S27, E0, not_3_out, E3, E4);
  and and_41 (and_41_out, not_1_out, E1, not_3_out, E3, E4);
  and and_42 (and_42_out, not_1_out, not_2_out, E2, E3, E4);
  and and_43 (and_43_out, E0, E1, not_3_out, E3, E4);
  and and_44 (and_44_out, E0, not_2_out, E2, E3, E4);
  and and_45 (and_45_out, not_1_out, E1, E2, E3, E4);
  and and_46 (and_46_out, not_1_out, not_2_out, E2, E3, E4);
  and and_47 (S31, E0, not_2_out, E2, E3, E4);
  or or_1 (s4, and_5_out, and_6_out);
  or or_2 (s5, and_7_out, and_8_out);
  or or_3 (s8, and_11_out, and_12_out);
  or or_4 (s9, and_13_out, and_14_out);
  or or_5 (s12, and_17_out, and_18_out);
  or or_6 (s13, and_19_out, and_20_out);
  or or_7 (S16, and_23_out, and_24_out);
  or or_8 (S17, and_25_out, and_26_out);
  or or_9 (s20, and_29_out, and_30_out);
  or or_10 (s21, and_31_out, and_32_out);
  or or_11 (s24, and_35_out, and_36_out);
  or or_12 (s25, and_37_out, and_38_out);
  or or_13 (S28, and_41_out, and_42_out);
  or or_14 (S29, and_43_out, and_44_out);
  or or_15 (S30, and_45_out, and_46_out);
endmodule

module RegistroDemovimientoNav (
  input  [31:0] in_1,
  input  E4,
  input  E3,
  input  E2,
  input  E1,
  input  E0,
  input  [31:0] in_7,
  output [31:0] out_8,
  output [31:0] out_9,
  output [31:0] out_10
);

  wire [31:0] rm_parte_inferior_1_out_6, rm_parte_superior_1_out_6;

  RM_Parte_Inferior rm_parte_inferior_1 (
    .E0(E0), .E1(E1), .E2(E2), .E3(E3), .E4(E4), .out_6(rm_parte_inferior_1_out_6[0]),
    .s1(rm_parte_inferior_1_out_6[1]), .s2(rm_parte_inferior_1_out_6[2]), .s3(rm_parte_inferior_1_out_6[3]),
    .s4(rm_parte_inferior_1_out_6[4]), .s5(rm_parte_inferior_1_out_6[5]), .s6(rm_parte_inferior_1_out_6[6]),
    .s7(rm_parte_inferior_1_out_6[7]), .s8(rm_parte_inferior_1_out_6[8]), .s9(rm_parte_inferior_1_out_6[9]),
    .s10(rm_parte_inferior_1_out_6[10]), .s11(rm_parte_inferior_1_out_6[11]),
    .s12(rm_parte_inferior_1_out_6[12]), .s13(rm_parte_inferior_1_out_6[13]),
    .s14(rm_parte_inferior_1_out_6[14]), .s15(rm_parte_inferior_1_out_6[15]),
    .S16(rm_parte_inferior_1_out_6[16]), .S17(rm_parte_inferior_1_out_6[17]),
    .S18(rm_parte_inferior_1_out_6[18]), .S19(rm_parte_inferior_1_out_6[19]),
    .s20(rm_parte_inferior_1_out_6[20]), .s21(rm_parte_inferior_1_out_6[21]),
    .s22(rm_parte_inferior_1_out_6[22]), .s23(rm_parte_inferior_1_out_6[23]),
    .s24(rm_parte_inferior_1_out_6[24]), .s25(rm_parte_inferior_1_out_6[25]),
    .s26(rm_parte_inferior_1_out_6[26]), .S27(rm_parte_inferior_1_out_6[27]),
    .S28(rm_parte_inferior_1_out_6[28]), .S29(rm_parte_inferior_1_out_6[29]),
    .S30(rm_parte_inferior_1_out_6[30]), .S31(rm_parte_inferior_1_out_6[31]));
  RM_Parte_superior rm_parte_superior_1 (
    .E0(E0), .E1(E1), .E2(E2), .E3(E3), .E4(E4), .out_6(rm_parte_superior_1_out_6[0]),
    .out_7(rm_parte_superior_1_out_6[1]), .out_8(rm_parte_superior_1_out_6[2]),
    .out_9(rm_parte_superior_1_out_6[3]), .out_10(rm_parte_superior_1_out_6[4]),
    .out_11(rm_parte_superior_1_out_6[5]), .out_12(rm_parte_superior_1_out_6[6]),
    .out_13(rm_parte_superior_1_out_6[7]), .out_14(rm_parte_superior_1_out_6[8]),
    .out_15(rm_parte_superior_1_out_6[9]), .out_16(rm_parte_superior_1_out_6[10]),
    .out_17(rm_parte_superior_1_out_6[11]), .out_18(rm_parte_superior_1_out_6[12]),
    .out_19(rm_parte_superior_1_out_6[13]), .out_20(rm_parte_superior_1_out_6[14]),
    .out_21(rm_parte_superior_1_out_6[15]), .out_22(rm_parte_superior_1_out_6[16]),
    .out_23(rm_parte_superior_1_out_6[17]), .out_24(rm_parte_superior_1_out_6[18]),
    .out_25(rm_parte_superior_1_out_6[19]), .out_26(rm_parte_superior_1_out_6[20]),
    .out_27(rm_parte_superior_1_out_6[21]), .out_28(rm_parte_superior_1_out_6[22]),
    .out_29(rm_parte_superior_1_out_6[23]), .out_30(rm_parte_superior_1_out_6[24]),
    .out_31(rm_parte_superior_1_out_6[25]), .out_32(rm_parte_superior_1_out_6[26]),
    .out_33(rm_parte_superior_1_out_6[27]), .out_34(rm_parte_superior_1_out_6[28]),
    .out_35(rm_parte_superior_1_out_6[29]), .out_36(rm_parte_superior_1_out_6[30]),
    .out_37(rm_parte_superior_1_out_6[31]));
  assign out_10 = rm_parte_superior_1_out_6 | in_7;  // OR_Gate or_1, 32 bits wide
  assign out_8 = rm_parte_inferior_1_out_6 | in_1;  // OR_Gate or_2, 32 bits wide
  assign out_9 = rm_parte_inferior_1_out_6 | rm_parte_superior_1_out_6;  // OR_Gate or_3, 32 bits wide

  // Other names for the same wires on the sheet: _1[31:0] = in_1; _2[31:0] = in_7
endmodule

module ContadorSRvida (
  input  in_1,
  input  in_2,
  input  in_3,
  output [1:0] out_4,
  output out_5,
  output out_6
);

  wire and_1_out, and_2_out, and_3_out, and_4_out;

  and and_1 (and_1_out, in_2, ~out_5, out_6);  // AND_Gate
  and and_2 (and_2_out, out_5, in_2, out_6);
  and and_3 (and_3_out, in_2, ~out_6);  // AND_Gate
  and and_4 (and_4_out, in_2, out_6);
  S_R_Flip_Flop s_r_ff_1 (.S(and_1_out), .clk(in_1), .R(and_2_out), .Q(out_5), .reset(in_3));  // open: Qn, preset, en
  S_R_Flip_Flop s_r_ff_2 (.S(and_3_out), .clk(in_1), .R(and_4_out), .Q(out_6), .reset(in_3));  // open: Qn, preset, en
  not not_1 (out_4[0], out_5);
  not not_2 (out_4[1], out_6);
endmodule

module Display (
  input  [1:0] in_1,
  output a,
  output b,
  output c,
  output d,
  output e,
  output f,
  output g
);

  wire not_1_out, not_2_out, not_3_out, not_5_out, not_6_out;

  not not_1 (not_1_out, in_1[0]);
  not not_2 (not_2_out, in_1[1]);
  not not_3 (not_3_out, in_1[0]);
  not not_4 (e, in_1[0]);
  not not_5 (not_5_out, in_1[1]);
  not not_6 (not_6_out, in_1[0]);
  or or_1 (a, not_1_out, in_1[1]);
  or or_2 (c, not_2_out, in_1[0]);
  or or_3 (d, not_3_out, in_1[1]);
  and and_1 (f, not_5_out, not_6_out);

  assign b = 1'b1;
  assign g = in_1[1];
endmodule

module Vida (
  input  Reloj,
  input  Entrada,
  input  Reset,
  output out_4,
  output out_5,
  output out_6,
  output out_7,
  output out_8,
  output out_9,
  output out_10,
  output out_11,
  output out_12
);

  wire [1:0] contadorsrvida_1_out_4;

  ContadorSRvida contadorsrvida_1 (
    .in_1(Reloj), .in_2(Entrada), .in_3(Reset), .out_4(contadorsrvida_1_out_4), .out_5(out_11), .out_6(out_12));
  Display display_1 (
    .in_1({contadorsrvida_1_out_4[0], contadorsrvida_1_out_4[1]}), .a(out_4), .b(out_5), .c(out_6),
    .d(out_7), .e(out_8), .f(out_9), .g(out_10));
endmodule

module colision (
  input  [31:0] in_1,
  input  [31:0] in_2,
  output out_3
);

  wire comparator_1_eq;
  wire [31:0] and_1_out;

  assign and_1_out = in_1 & in_2;  // AND_Gate and_1, 32 bits wide
  Comparator #(.width(32)) comparator_1 (.a({32{1'b0}}), .b(and_1_out), .eq(comparator_1_eq));  // open: gt, lt
  not not_1 (out_3, comparator_1_eq);
endmodule

module CPU (
  input  in_1,
  input  in_2,
  input  in_3,
  output enable,
  output clear,
  output vida
);

  wire and_1_out, and_2_out, and_3_out, and_4_out, or_1_out, s_r_ff_1_q, s_r_ff_1_qn, s_r_ff_2_q, s_r_ff_2_qn;

  and and_1 (and_1_out, in_1, s_r_ff_1_qn, s_r_ff_2_qn);
  and and_2 (and_2_out, s_r_ff_1_q, s_r_ff_2_q);
  and and_3 (and_3_out, s_r_ff_1_q, s_r_ff_2_qn);
  and and_4 (and_4_out, s_r_ff_2_q, s_r_ff_1_qn);
  S_R_Flip_Flop s_r_ff_1 (
    .S(and_4_out), .clk(in_3), .R(and_2_out), .Q(s_r_ff_1_q), .Qn(s_r_ff_1_qn), .reset(in_2), .en(in_3));  // open: preset
  S_R_Flip_Flop s_r_ff_2 (
    .S(or_1_out), .clk(in_3), .R(s_r_ff_2_q), .Q(s_r_ff_2_q), .Qn(s_r_ff_2_qn), .reset(in_2), .en(in_3));  // open: preset
  or or_1 (or_1_out, and_1_out, and_3_out);
  and and_5 (enable, s_r_ff_1_qn, s_r_ff_2_qn);
  and and_6 (clear, s_r_ff_1_q, s_r_ff_2_qn);
  and and_7 (vida, s_r_ff_1_q, s_r_ff_2_q);

  // Notes on the sheet:
  //   1
  //   0
endmodule
