// Logisim project TEST.circ as structural Verilog: 9 circuits, main circuit main
module main (
  input  in_1,
  input  in_2,
  input  in_3,
  input  in_4,
  input  in_5,
  input  in_6,
  input  CLEAR_MEM,
  output [31:0] out_8
);

  wire ALUsrc, and_1_out, and_2_out, and_3_out, and_4_out, and_6_out, Branch, cien, clk, HALT, jr, jump,
       memRead, memToreg, memWrite, not_1_out, not_2_out, not_3_out, not_4_out, not_5_out, not_6_out,
       not_7_out, not_8_out, not_9_out, not_10_out, not_11_out, not_12_out, op0, op1, or_1_out, or_2_out,
       or_3_out, or_4_out, or_5_out, OUT, regDST, regWrite, save, zero;
  wire [1:0] aluA;
  wire [2:0] ALU_cpu_x;
  wire [4:0] multiplexer_1_out, multiplexer_2_out;
  wire [23:0] adder_1_out, adder_2_out, multiplexer_8_out, multiplexer_9_out, n32to24_1_out_2,
       n32to24_2_out_2, n32to24_3_out_2, PC, register_1_q;
  wire [31:0] alu32bits_1_salida, BANCO_REG_out_8, BANCO_REG_out_9, bit_extender_1_out, display_1_out_5,
       display_1_out_6, display_1_out_7, display_1_out_8, display_1_out_9, display_1_out_10,
       display_1_out_11, display_1_out_12, display_1_out_13, display_1_out_14, display_1_out_15,
       display_1_out_16, display_1_out_17, display_1_out_18, display_1_out_19, display_1_out_20,
       display_1_out_21, display_1_out_22, display_1_out_23, display_1_out_24, display_1_out_25,
       display_1_out_26, display_1_out_27, display_1_out_28, display_1_out_29, display_1_out_30,
       display_1_out_31, display_1_out_32, display_1_out_33, display_1_out_34, display_1_out_35,
       display_1_out_36, multiplexer_3_out, multiplexer_5_out, multiplexer_6_out, multiplexer_7_out,
       multiplexer_10_out, ram_1_data, sign_extend_1_out_2;

  not not_1 (not_1_out, HALT);
  not not_2 (not_2_out, out_8[31]);
  CPU3 cpu3_1 (
    .in_1(out_8[31]), .in_2(out_8[30]), .in_3(out_8[29]), .in_4(out_8[28]), .in_5(out_8[27]),
    .in_6(out_8[26]), ._100100(cien), .ZERO(zero), .CLOCK(clk), .RESET(in_6), .save(save), .jr(jr),
    .RedDst(regDST), .ALUSrc(ALUsrc), .memToReg(memToreg), .regWrite(regWrite), .memRead(memRead),
    .memWrite(memWrite), .Branch(Branch), .ALUop1(op1), .ALUop0(op0), .Jump(jump), .ALU_A(aluA), .HALT(HALT),
    .OUT(OUT));
  Register #(.width(24)) register_1 (.D(PC), .en(and_1_out), .Q(register_1_q), .clk(and_1_out), .clr(in_6));
  and and_1 (and_1_out, not_1_out, clk);
  and and_2 (and_2_out, not_2_out, not_3_out, out_8[29], not_4_out, not_6_out, not_5_out);
  not not_3 (not_3_out, out_8[30]);
  not not_4 (not_4_out, out_8[28]);
  not not_5 (not_5_out, out_8[26]);
  not not_6 (not_6_out, out_8[27]);
  not not_7 (not_7_out, out_8[25]);
  Clock clock_1 (.out(clk));
  and and_3 (and_3_out, not_10_out, not_9_out, out_8[18], not_8_out, out_8[16]);
  and and_4 (and_4_out, not_7_out, not_12_out, out_8[23], not_11_out, out_8[21]);
  not not_8 (not_8_out, out_8[17]);
  not not_9 (not_9_out, out_8[19]);
  not not_10 (not_10_out, out_8[20]);
  not not_11 (not_11_out, out_8[22]);
  not not_12 (not_12_out, out_8[24]);
  Adder #(.width(24)) adder_1 (.a(24'h1), .b(register_1_q), .out(adder_1_out));  // open: cin, cout
  and and_5 (cien, and_2_out, and_4_out, and_3_out);
  ROM #(.addrWidth(24), .dataWidth(32)) rom_1 (.addr(register_1_q), .data(out_8), .sel(in_4));
  or or_1 (or_1_out, regWrite, save);
  Multiplexer #(.width(5), .enable("false")) multiplexer_1 (
    .in0(out_8[20:16]), .in1(out_8[15:11]), .out(multiplexer_1_out), .sel(regDST));
  Multiplexer #(.width(5), .enable("false")) multiplexer_2 (
    .in0(multiplexer_1_out), .in1({5{1'b1}}), .out(multiplexer_2_out), .sel(save));
  Multiplexer #(.width(32), .enable("false")) multiplexer_3 (
    .in0(multiplexer_7_out), .in1(bit_extender_1_out), .out(multiplexer_3_out), .sel(save));
  assign bit_extender_1_out = {{8{1'b0}}, adder_1_out};  // Bit_Extender bit_extender_1
  Multiplexer #(.width(24), .enable("false")) multiplexer_4 (
    .in0(multiplexer_9_out), .in1(n32to24_1_out_2), .out(PC), .sel(jr));
  _32to24 u_32to24_1 (.in_1(BANCO_REG_out_8), .out_2(n32to24_1_out_2));
  BancoReg BANCO_REG (
    .in_1(out_8[25:21]), .in_2(out_8[20:16]), .in_3(multiplexer_2_out), .in_4(multiplexer_3_out),
    .write(or_1_out), .clock(clk), .Reset_all(in_6), .out_8(BANCO_REG_out_8), .out_9(BANCO_REG_out_9));
  Multiplexer #(.width(32), .enable("false")) multiplexer_5 (
    .in0(BANCO_REG_out_9), .in1(sign_extend_1_out_2), .out(multiplexer_5_out), .sel(ALUsrc));
  sign_extend sign_extend_1 (.in_1(out_8[15:0]), .out_2(sign_extend_1_out_2));
  _32to24 u_32to24_2 (.in_1(sign_extend_1_out_2), .out_2(n32to24_2_out_2));
  Multiplexer #(.select(2), .width(32), .enable("false")) multiplexer_6 (
    .in0(BANCO_REG_out_8), .in1(BANCO_REG_out_9), .in2(32'h1), .out(multiplexer_6_out), .sel(aluA));  // open: in3
  Alu32bits alu32bits_1 (
    .Salida(alu32bits_1_salida), .zero(zero), .A(multiplexer_6_out), .B(multiplexer_5_out), .Select(ALU_cpu_x));  // open: Overflow
  AluControl ALU_cpu (.in_1({op1, op0}), .in_2(out_8[5:0]), .x(ALU_cpu_x));  // open: j
  Multiplexer #(.width(32), .enable("false")) multiplexer_7 (
    .in0(alu32bits_1_salida), .in1(ram_1_data), .out(multiplexer_7_out), .sel(memToreg));
  Multiplexer #(.width(24), .enable("false")) multiplexer_8 (
    .in0(adder_1_out), .in1(adder_2_out), .out(multiplexer_8_out), .sel(and_6_out));
  Adder #(.width(24)) adder_2 (.a(adder_1_out), .b(n32to24_2_out_2), .out(adder_2_out));  // open: cin, cout
  and and_6 (and_6_out, Branch, zero);
  _32to24 u_32to24_3 (.in_1(alu32bits_1_salida), .out_2(n32to24_3_out_2));
  Multiplexer #(.width(24), .enable("false")) multiplexer_9 (
    .in0(multiplexer_8_out), .in1(out_8[23:0]), .out(multiplexer_9_out), .sel(jump));
  or or_2 (or_2_out, memRead, in_5, memWrite);
  or or_3 (or_3_out, in_3, memWrite);
  or or_4 (or_4_out, memRead, in_1);
  RAM #(.addrWidth(24), .dataWidth(32), .bus("separate")) ram_1 (
    .addr(n32to24_3_out_2), .din(BANCO_REG_out_9), .data(ram_1_data), .str(or_3_out), .sel(or_2_out),
    .clk(or_5_out), .ld(or_4_out), .clr(CLEAR_MEM));
  or or_5 (or_5_out, clk, in_2);
  Multiplexer #(.width(32), .enable("false")) multiplexer_10 (
    .in0({32{1'b0}}), .in1(ram_1_data), .out(multiplexer_10_out), .sel(OUT));
  DotMatrix #(.inputtype("row"), .matrixcols(32), .matrixrows(32)) dotmatrix_1 (
    .row0(display_1_out_5), .row1(display_1_out_6), .row2(display_1_out_7), .row3(display_1_out_8),
    .row4(display_1_out_9), .row5(display_1_out_10), .row6(display_1_out_11), .row7(display_1_out_12),
    .row8(display_1_out_13), .row9(display_1_out_14), .row10(display_1_out_15), .row11(display_1_out_16),
    .row12(display_1_out_17), .row13(display_1_out_18), .row14(display_1_out_19), .row15(display_1_out_20),
    .row16(display_1_out_21), .row17(display_1_out_22), .row18(display_1_out_23), .row19(display_1_out_24),
    .row20(display_1_out_25), .row21(display_1_out_26), .row22(display_1_out_27), .row23(display_1_out_28),
    .row24(display_1_out_29), .row25(display_1_out_30), .row26(display_1_out_31), .row27(display_1_out_32),
    .row28(display_1_out_33), .row29(display_1_out_34), .row30(display_1_out_35), .row31(display_1_out_36));
  Lab__Version_prueba_display display_1 (
    .in_1(multiplexer_10_out), .in_3(clk), .in_4(in_6), .out_5(display_1_out_5), .out_6(display_1_out_6),
    .out_7(display_1_out_7), .out_8(display_1_out_8), .out_9(display_1_out_9), .out_10(display_1_out_10),
    .out_11(display_1_out_11), .out_12(display_1_out_12), .out_13(display_1_out_13),
    .out_14(display_1_out_14), .out_15(display_1_out_15), .out_16(display_1_out_16),
    .out_17(display_1_out_17), .out_18(display_1_out_18), .out_19(display_1_out_19),
    .out_20(display_1_out_20), .out_21(display_1_out_21), .out_22(display_1_out_22),
    .out_23(display_1_out_23), .out_24(display_1_out_24), .out_25(display_1_out_25),
    .out_26(display_1_out_26), .out_27(display_1_out_27), .out_28(display_1_out_28),
    .out_29(display_1_out_29), .out_30(display_1_out_30), .out_31(display_1_out_31),
    .out_32(display_1_out_32), .out_33(display_1_out_33), .out_34(display_1_out_34),
    .out_35(display_1_out_35), .out_36(display_1_out_36));  // open: in_2

  // Other names for the same wires on the sheet: _0_5[5:0] = out_8[5:0]; _15_0[15:0] = out_8[15:0];
  //   _20_16[4:0] = out_8[20:16]; _25_21[4:0] = out_8[25:21]; clr = in_6; cpu[5:0] = out_8[31:26];
  //   _15_11[4:0] = out_8[15:11]

  // Notes on the sheet:
  //   contents of rom_1 (hex, n*v repeats v):
  //   c000002 c00000d 22100000 22310001 22730000 21080032 12280005 2118020 ae700010 22730001 22310001
  //   8000006 ffe00000 2008002f 20090001 200a0000 200b0001 20100000 11680008 21440000 ae040064 214c0000
  //   1495020 21890000 216b0001 22100001 8000012 0 20a50032 90b90010 20a5fffd 90ba0064
  //   en JAL=1
  //   32/24
  //   sign-ext
  //   32/24
  //   32to24
  //   OUTPUT ASYNC 
  //   INPUT SYNCRONIC
endmodule

module BancoReg (
  input  [4:0] in_1,
  input  [4:0] in_2,
  input  [4:0] in_3,
  input  [31:0] in_4,
  input  write,
  input  clock,
  input  Reset_all,
  output [31:0] out_8,
  output [31:0] out_9
);

  wire _0, _1, _2, _3, _4, _5, _6, _7, _8, _9, _10, _11, _12, _13, _14, _15, _16, _17, _18, _19, _20, _21,
       _22, _23, _24, _25, _26, _27, _28, _29, _30, _31, and_1_out, and_2_out, and_3_out, and_4_out,
       and_5_out, and_6_out, and_7_out, and_8_out, and_9_out, and_10_out, and_11_out, and_12_out, and_13_out,
       and_14_out, and_15_out, and_16_out, and_17_out, and_18_out, and_19_out, and_20_out, and_21_out,
       and_22_out, and_23_out, and_24_out, and_25_out, and_26_out, and_27_out, and_28_out, and_29_out,
       and_30_out, and_31_out;
  wire [31:0] register_1_q, register_2_q, register_3_q, register_4_q, register_5_q, register_6_q,
       register_7_q, register_8_q, register_9_q, register_10_q, register_11_q, register_12_q, register_13_q,
       register_14_q, register_15_q, register_17_q, register_18_q, register_19_q, register_20_q,
       register_21_q, register_22_q, register_23_q, register_24_q, register_25_q, register_26_q,
       register_27_q, register_28_q, register_29_q, register_30_q, register_31_q, x;

  Decoder #(.select(5), .enable("false")) decoder_1 (
    .out0(_0), .out1(_1), .out2(_2), .out3(_3), .out4(_4), .out5(_5), .out6(_6), .out7(_7), .out8(_8),
    .out9(_9), .out10(_10), .out11(_11), .out12(_12), .out13(_13), .out14(_14), .out15(_15), .out16(_16),
    .out17(_17), .out18(_18), .out19(_19), .out20(_20), .out21(_21), .out22(_22), .out23(_23), .out24(_24),
    .out25(_25), .out26(_26), .out27(_27), .out28(_28), .out29(_29), .out30(_30), .out31(_31), .sel(in_3));
  and and_1 (and_1_out, _1, write);
  and and_2 (and_2_out, _2, write);
  and and_3 (and_3_out, _3, write);
  and and_4 (and_4_out, _4, write);
  and and_5 (and_5_out, _5, write);
  and and_6 (and_6_out, _6, write);
  and and_7 (and_7_out, _7, write);
  and and_8 (and_8_out, _8, write);
  and and_9 (and_9_out, _9, write);
  and and_10 (and_10_out, _10, write);
  and and_11 (and_11_out, _11, write);
  and and_12 (and_12_out, _12, write);
  and and_13 (and_13_out, _13, write);
  and and_14 (and_14_out, _14, write);
  and and_15 (and_15_out, _15, write);
  and and_16 (and_16_out, _16, write);
  and and_17 (and_17_out, _17, write);
  and and_18 (and_18_out, _18, write);
  and and_19 (and_19_out, _19, write);
  and and_20 (and_20_out, _20, write);
  and and_21 (and_21_out, _21, write);
  and and_22 (and_22_out, _22, write);
  and and_23 (and_23_out, _23, write);
  and and_24 (and_24_out, _24, write);
  and and_25 (and_25_out, _25, write);
  and and_26 (and_26_out, _26, write);
  and and_27 (and_27_out, _27, write);
  and and_28 (and_28_out, _28, write);
  and and_29 (and_29_out, _29, write);
  and and_30 (and_30_out, _30, write);
  and and_31 (and_31_out, _31, write);
  Register #(.width(32)) register_1 (.D(in_4), .en(and_1_out), .Q(register_1_q), .clk(clock), .clr(Reset_all));
  Register #(.width(32)) register_2 (.D(in_4), .en(and_2_out), .Q(register_2_q), .clk(clock), .clr(Reset_all));
  Register #(.width(32)) register_3 (.D(in_4), .en(and_3_out), .Q(register_3_q), .clk(clock), .clr(Reset_all));
  Register #(.width(32)) register_4 (.D(in_4), .en(and_4_out), .Q(register_4_q), .clk(clock), .clr(Reset_all));
  Register #(.width(32)) register_5 (.D(in_4), .en(and_5_out), .Q(register_5_q), .clk(clock), .clr(Reset_all));
  Register #(.width(32)) register_6 (.D(in_4), .en(and_6_out), .Q(register_6_q), .clk(clock), .clr(Reset_all));
  Register #(.width(32)) register_7 (.D(in_4), .en(and_7_out), .Q(register_7_q), .clk(clock), .clr(Reset_all));
  Register #(.width(32)) register_8 (.D(in_4), .en(and_8_out), .Q(register_8_q), .clk(clock), .clr(Reset_all));
  Register #(.width(32)) register_9 (.D(in_4), .en(and_9_out), .Q(register_9_q), .clk(clock), .clr(Reset_all));
  Register #(.width(32)) register_10 (.D(in_4), .en(and_10_out), .Q(register_10_q), .clk(clock), .clr(Reset_all));
  Register #(.width(32)) register_11 (.D(in_4), .en(and_11_out), .Q(register_11_q), .clk(clock), .clr(Reset_all));
  Register #(.width(32)) register_12 (.D(in_4), .en(and_12_out), .Q(register_12_q), .clk(clock), .clr(Reset_all));
  Register #(.width(32)) register_13 (.D(in_4), .en(and_13_out), .Q(register_13_q), .clk(clock), .clr(Reset_all));
  Register #(.width(32)) register_14 (.D(in_4), .en(and_14_out), .Q(register_14_q), .clk(clock), .clr(Reset_all));
  Register #(.width(32)) register_15 (.D(in_4), .en(and_15_out), .Q(register_15_q), .clk(clock), .clr(Reset_all));
  Register #(.width(32)) register_16 (.D(in_4), .en(and_16_out), .Q(x), .clk(clock), .clr(Reset_all));
  Register #(.width(32)) register_17 (.D(in_4), .en(and_17_out), .Q(register_17_q), .clk(clock), .clr(Reset_all));
  Register #(.width(32)) register_18 (.D(in_4), .en(and_18_out), .Q(register_18_q), .clk(clock), .clr(Reset_all));
  Register #(.width(32)) register_19 (.D(in_4), .en(and_19_out), .Q(register_19_q), .clk(clock), .clr(Reset_all));
  Register #(.width(32)) register_20 (.D(in_4), .en(and_20_out), .Q(register_20_q), .clk(clock), .clr(Reset_all));
  Register #(.width(32)) register_21 (.D(in_4), .en(and_21_out), .Q(register_21_q), .clk(clock), .clr(Reset_all));
  Register #(.width(32)) register_22 (.D(in_4), .en(and_22_out), .Q(register_22_q), .clk(clock), .clr(Reset_all));
  Register #(.width(32)) register_23 (.D(in_4), .en(and_23_out), .Q(register_23_q), .clk(clock), .clr(Reset_all));
  Register #(.width(32)) register_24 (.D(in_4), .en(and_24_out), .Q(register_24_q), .clk(clock), .clr(Reset_all));
  Register #(.width(32)) register_25 (.D(in_4), .en(and_25_out), .Q(register_25_q), .clk(clock), .clr(Reset_all));
  Register #(.width(32)) register_26 (.D(in_4), .en(and_26_out), .Q(register_26_q), .clk(clock), .clr(Reset_all));
  Register #(.width(32)) register_27 (.D(in_4), .en(and_27_out), .Q(register_27_q), .clk(clock), .clr(Reset_all));
  Register #(.width(32)) register_28 (.D(in_4), .en(and_28_out), .Q(register_28_q), .clk(clock), .clr(Reset_all));
  Register #(.width(32)) register_29 (.D(in_4), .en(and_29_out), .Q(register_29_q), .clk(clock), .clr(Reset_all));
  Register #(.width(32)) register_30 (.D(in_4), .en(and_30_out), .Q(register_30_q), .clk(clock), .clr(Reset_all));
  Register #(.width(32)) register_31 (.D(in_4), .en(and_31_out), .Q(register_31_q), .clk(clock), .clr(Reset_all));
  Multiplexer #(.select(5), .width(32), .enable("false")) multiplexer_1 (
    .in0({32{1'b0}}), .in1(register_1_q), .in2(register_2_q), .in3(register_3_q), .in4(register_4_q),
    .in5(register_5_q), .in6(register_6_q), .in7(register_7_q), .in8(register_8_q), .in9(register_9_q),
    .in10(register_10_q), .in11(register_11_q), .in12(register_12_q), .in13(register_13_q),
    .in14(register_14_q), .in15(register_15_q), .in16(x), .in17(register_17_q), .in18(register_18_q),
    .in19(register_19_q), .in20(register_20_q), .in21(register_21_q), .in22(register_22_q),
    .in23(register_23_q), .in24(register_24_q), .in25(register_25_q), .in26(register_26_q),
    .in27(register_27_q), .in28(register_28_q), .in29(register_29_q), .in30(register_30_q),
    .in31(register_31_q), .out(out_8), .sel(in_1));
  Multiplexer #(.select(5), .width(32), .enable("false")) multiplexer_2 (
    .in0({32{1'b0}}), .in1(register_1_q), .in2(register_2_q), .in3(register_3_q), .in4(register_4_q),
    .in5(register_5_q), .in6(register_6_q), .in7(register_7_q), .in8(register_8_q), .in9(register_9_q),
    .in10(register_10_q), .in11(register_11_q), .in12(register_12_q), .in13(register_13_q),
    .in14(register_14_q), .in15(register_15_q), .in16(x), .in17(register_17_q), .in18(register_18_q),
    .in19(register_19_q), .in20(register_20_q), .in21(register_21_q), .in22(register_22_q),
    .in23(register_23_q), .in24(register_24_q), .in25(register_25_q), .in26(register_26_q),
    .in27(register_27_q), .in28(register_28_q), .in29(register_29_q), .in30(register_30_q),
    .in31(register_31_q), .out(out_9), .sel(in_2));

  // Other names for the same wires on the sheet: in[31:0] = in_4; out1[31:0] = out_8; out2[31:0] = out_9;
  //   read1[4:0] = in_1; read2[4:0] = in_2; reset = Reset_all; w = write

  // Notes on the sheet:
  //   Reg read1
  //   Reg read2
  //   Reg select
  //   input
endmodule

module sign_extend (
  input  [15:0] in_1,
  output [31:0] out_2
);


  assign out_2 = {{17{in_1[15]}}, in_1[14:0]};
endmodule

module shif_left2_26_to_28 (
  input  [25:0] in_1,
  output [27:0] out_2
);


  assign out_2 = {in_1, 2'b00};
endmodule

module _32to24 (
  input  [31:0] in_1,
  output [23:0] out_2
);


  assign out_2 = in_1[23:0];
endmodule

module CPU (
  input  i0,
  input  i1,
  input  i2,
  input  i3,
  input  i4,
  input  i5,
  output RedDst,
  output ALUSrc,
  output memToReg,
  output regWrite,
  output memRead,
  output memWrite,
  output Branch,
  output ALUop1,
  output ALUop0,
  output Jump
);

  wire not_2_out, not_3_out, not_4_out, not_5_out, not_6_out, not_7_out, not_8_out, not_9_out, not_10_out,
       not_11_out;

  not not_1 (RedDst, i4);
  not not_2 (not_2_out, i2);
  not not_3 (not_3_out, i3);
  not not_4 (not_4_out, i2);
  not not_5 (not_5_out, i3);
  not not_6 (not_6_out, i4);
  not not_7 (not_7_out, i0);
  not not_8 (not_8_out, i1);
  not not_9 (not_9_out, i2);
  not not_10 (not_10_out, i3);
  not not_11 (not_11_out, i5);
  and and_1 (regWrite, not_2_out, not_3_out);
  and and_2 (memRead, not_4_out, i4);
  and and_3 (ALUop1, not_5_out, not_6_out);
  and and_4 (Jump, not_7_out, not_8_out, not_9_out, not_10_out, i4, not_11_out);

  assign ALUop0 = i3;
  assign ALUSrc = i4;
  assign Branch = i3;
  assign memToReg = i4;
  assign memWrite = i2;
endmodule

module CPU2 (
  input  i0,
  input  i1,
  input  i2,
  input  i3,
  input  i4,
  input  i5,
  output save,
  output jr,
  output RedDst,
  output ALUSrc,
  output memToReg,
  output regWrite,
  output memRead,
  output memWrite,
  output Branch,
  output ALUop1,
  output ALUop0,
  output Jump
);

  wire and_3_out, and_4_out, and_5_out, and_6_out, and_7_out, and_8_out, and_9_out, and_10_out, and_11_out,
       and_12_out, and_13_out, and_14_out, and_15_out, and_16_out, and_17_out, and_18_out, and_19_out,
       and_20_out, and_21_out, and_22_out, and_23_out, and_24_out, and_25_out, and_26_out, and_27_out,
       and_28_out, and_29_out, and_30_out, and_31_out, not_1_out, not_2_out, not_3_out, not_4_out, not_5_out,
       not_6_out, not_7_out, not_8_out, not_9_out, not_10_out, not_11_out, not_12_out, not_13_out,
       not_14_out, not_15_out, not_16_out, not_17_out, not_18_out, not_19_out, not_20_out, not_21_out,
       not_22_out, not_23_out, not_24_out, not_25_out, not_26_out, not_27_out, not_28_out, not_29_out,
       not_30_out, not_31_out, not_32_out, not_33_out, not_34_out, not_35_out, not_36_out, not_37_out,
       not_38_out, not_39_out, not_40_out, not_41_out, not_42_out, not_43_out, not_44_out, not_45_out,
       not_46_out, not_47_out, not_48_out, not_49_out;

  not not_1 (not_1_out, i0);
  not not_2 (not_2_out, i1);
  not not_3 (not_3_out, i2);
  not not_4 (not_4_out, i3);
  and and_1 (jr, i0, i1, i2, i3, i4, i5);
  not not_5 (not_5_out, i2);
  not not_6 (not_6_out, i4);
  not not_7 (not_7_out, i4);
  not not_8 (not_8_out, i4);
  not not_9 (not_9_out, i4);
  not not_10 (not_10_out, i4);
  not not_11 (not_11_out, i0);
  not not_12 (not_12_out, i1);
  not not_13 (not_13_out, i3);
  not not_14 (not_14_out, i5);
  not not_15 (not_15_out, i0);
  not not_16 (not_16_out, i1);
  not not_17 (not_17_out, i3);
  not not_18 (not_18_out, i4);
  not not_19 (not_19_out, i5);
  not not_20 (not_20_out, i2);
  not not_21 (not_21_out, i3);
  not not_22 (not_22_out, i2);
  not not_23 (not_23_out, i3);
  not not_24 (not_24_out, i2);
  not not_25 (not_25_out, i3);
  not not_26 (not_26_out, i2);
  not not_27 (not_27_out, i2);
  not not_28 (not_28_out, i2);
  not not_29 (not_29_out, i1);
  not not_30 (not_30_out, i1);
  not not_31 (not_31_out, i0);
  not not_32 (not_32_out, i3);
  not not_33 (not_33_out, i1);
  not not_34 (not_34_out, i4);
  not not_35 (not_35_out, i5);
  not not_36 (not_36_out, i0);
  not not_37 (not_37_out, i2);
  not not_38 (not_38_out, i3);
  not not_39 (not_39_out, i4);
  not not_40 (not_40_out, i3);
  not not_41 (not_41_out, i4);
  not not_42 (not_42_out, i3);
  not not_43 (not_43_out, i4);
  not not_44 (not_44_out, i3);
  not not_45 (not_45_out, i4);
  not not_46 (not_46_out, i0);
  not not_47 (not_47_out, i1);
  not not_48 (not_48_out, i2);
  not not_49 (not_49_out, i3);
  and and_2 (save, not_1_out, not_2_out, not_3_out, not_4_out, i4, i5);
  and and_3 (and_3_out, not_5_out, not_6_out);
  and and_4 (and_4_out, not_7_out, i5);
  and and_5 (and_5_out, i3, not_8_out);
  and and_6 (and_6_out, i1, not_9_out);
  and and_7 (and_7_out, i0, not_10_out);
  and and_8 (and_8_out, not_11_out, not_12_out, i2, not_13_out, not_14_out);
  and and_9 (and_9_out, not_15_out, not_16_out, not_17_out, not_18_out, not_19_out);
  and and_10 (and_10_out, not_20_out, not_21_out, i5);
  and and_11 (and_11_out, i1, not_22_out, not_23_out);
  and and_12 (and_12_out, i0, not_24_out, not_25_out);
  and and_13 (and_13_out, not_26_out, i3, i4);
  and and_14 (and_14_out, i1, not_27_out, i4);
  and and_15 (and_15_out, i0, not_28_out, i4);
  and and_16 (and_16_out, not_29_out, i2, i5);
  and and_17 (and_17_out, not_30_out, i2, i4);
  and and_18 (and_18_out, not_31_out, i2, i3);
  and and_19 (and_19_out, i1, i2, not_32_out);
  and and_20 (and_20_out, i0, not_33_out, i2);
  and and_21 (and_21_out, i0, i2, not_34_out);
  and and_22 (and_22_out, i0, i2, not_35_out);
  and and_23 (and_23_out, not_36_out, i3);
  and and_24 (and_24_out, i3, i5);
  and and_25 (and_25_out, i3, i4);
  and and_26 (and_26_out, i2, i3);
  and and_27 (and_27_out, i1, i3);
  and and_28 (and_28_out, not_37_out, not_38_out, not_39_out);
  and and_29 (and_29_out, not_40_out, not_41_out, i5);
  and and_30 (and_30_out, i1, not_42_out, not_43_out);
  and and_31 (and_31_out, i0, not_44_out, not_45_out);
  and and_32 (Jump, not_46_out, not_47_out, not_48_out, not_49_out, i4);
  or or_1 (RedDst, and_3_out, and_4_out, and_5_out, and_6_out, and_7_out);
  or or_2 (ALUSrc, i4, and_8_out);
  or or_3 (regWrite, and_9_out, and_10_out, and_11_out, and_12_out);
  or or_4 (memRead, and_13_out, and_14_out, and_15_out);
  or or_5 (memWrite, and_16_out, and_17_out, and_18_out, and_19_out, and_20_out, and_21_out, and_22_out);
  or or_6 (Branch, and_23_out, and_24_out, and_25_out, and_26_out, and_27_out);
  or or_7 (ALUop1, and_28_out, and_29_out, and_30_out, and_31_out);

  assign ALUop0 = i3;
  assign memToReg = i4;
endmodule

module display (
  input  in_1,
  input  in_2,
  input  in_3,
  input  [31:0] in_4
);

  wire [31:0] display_1_out_5, display_1_out_6, display_1_out_7, display_1_out_8, display_1_out_9,
       display_1_out_10, display_1_out_11, display_1_out_12, display_1_out_13, display_1_out_14,
       display_1_out_15, display_1_out_16, display_1_out_17, display_1_out_18, display_1_out_19,
       display_1_out_20, display_1_out_21, display_1_out_22, display_1_out_23, display_1_out_24,
       display_1_out_25, display_1_out_26, display_1_out_27, display_1_out_28, display_1_out_29,
       display_1_out_30, display_1_out_31, display_1_out_32, display_1_out_33, display_1_out_34,
       display_1_out_35, display_1_out_36;

  Lab__Version_prueba_display display_1 (
    .in_1(in_4), .in_2(in_3), .in_3(in_2), .in_4(in_1), .out_5(display_1_out_5), .out_6(display_1_out_6),
    .out_7(display_1_out_7), .out_8(display_1_out_8), .out_9(display_1_out_9), .out_10(display_1_out_10),
    .out_11(display_1_out_11), .out_12(display_1_out_12), .out_13(display_1_out_13),
    .out_14(display_1_out_14), .out_15(display_1_out_15), .out_16(display_1_out_16),
    .out_17(display_1_out_17), .out_18(display_1_out_18), .out_19(display_1_out_19),
    .out_20(display_1_out_20), .out_21(display_1_out_21), .out_22(display_1_out_22),
    .out_23(display_1_out_23), .out_24(display_1_out_24), .out_25(display_1_out_25),
    .out_26(display_1_out_26), .out_27(display_1_out_27), .out_28(display_1_out_28),
    .out_29(display_1_out_29), .out_30(display_1_out_30), .out_31(display_1_out_31),
    .out_32(display_1_out_32), .out_33(display_1_out_33), .out_34(display_1_out_34),
    .out_35(display_1_out_35), .out_36(display_1_out_36));
  DotMatrix #(.inputtype("row"), .matrixcols(32), .matrixrows(32)) dotmatrix_1 (
    .row0(display_1_out_5), .row1(display_1_out_6), .row2(display_1_out_7), .row3(display_1_out_8),
    .row4(display_1_out_9), .row5(display_1_out_10), .row6(display_1_out_11), .row7(display_1_out_12),
    .row8(display_1_out_13), .row9(display_1_out_14), .row10(display_1_out_15), .row11(display_1_out_16),
    .row12(display_1_out_17), .row13(display_1_out_18), .row14(display_1_out_19), .row15(display_1_out_20),
    .row16(display_1_out_21), .row17(display_1_out_22), .row18(display_1_out_23), .row19(display_1_out_24),
    .row20(display_1_out_25), .row21(display_1_out_26), .row22(display_1_out_27), .row23(display_1_out_28),
    .row24(display_1_out_29), .row25(display_1_out_30), .row26(display_1_out_31), .row27(display_1_out_32),
    .row28(display_1_out_33), .row29(display_1_out_34), .row30(display_1_out_35), .row31(display_1_out_36));
endmodule

module CPU3 (
  input  in_1,
  input  in_2,
  input  in_3,
  input  in_4,
  input  in_5,
  input  in_6,
  input  _100100,
  input  ZERO,
  input  CLOCK,
  input  RESET,
  output save,
  output jr,
  output RedDst,
  output ALUSrc,
  output memToReg,
  output regWrite,
  output memRead,
  output memWrite,
  output Branch,
  output ALUop1,
  output ALUop0,
  output Jump,
  output [1:0] ALU_A,
  output HALT,
  output OUT
);

  wire _0, _2, and_1_out, and_2_out, and_3_out, and_4_out, and_5_out, cpu2_1_aluop0, cpu2_1_aluop1,
       cpu2_1_alusrc, cpu2_1_branch, cpu2_1_jr, cpu2_1_jump, cpu2_1_memread, cpu2_1_memtoreg,
       cpu2_1_memwrite, cpu2_1_reddst, cpu2_1_regwrite, cpu2_1_save, not_1_out, or_1_out, or_2_out, or_3_out,
       or_4_out, or_5_out, s_r_ff_1_q, s_r_ff_1_qn, s_r_ff_2_q, s_r_ff_2_qn, transistor_1_out;
  wire [1:0] multiplexer_1_out;

  Transistor #(.\type ("n")) transistor_1 (.in(1'b0), .out(transistor_1_out), .gate(_2));
  CPU2 cpu2_1 (
    .i0(in_1), .i1(in_2), .i2(in_3), .i3(in_4), .i4(in_5), .i5(in_6), .save(cpu2_1_save), .jr(cpu2_1_jr),
    .RedDst(cpu2_1_reddst), .ALUSrc(cpu2_1_alusrc), .memToReg(cpu2_1_memtoreg), .regWrite(cpu2_1_regwrite),
    .memRead(cpu2_1_memread), .memWrite(cpu2_1_memwrite), .Branch(cpu2_1_branch), .ALUop1(cpu2_1_aluop1),
    .ALUop0(cpu2_1_aluop0), .Jump(cpu2_1_jump));
  or or_1 (or_1_out, OUT, 1'b0);
  Multiplexer #(.select(2), .width(2), .enable("false")) multiplexer_1 (
    .in0(2'b00), .in1(2'b01), .in2(2'b10), .in3(2'b00), .out(multiplexer_1_out), .sel({_2, OUT}));
  Multiplexer #(.enable("false")) multiplexer_2 (.in0(cpu2_1_save), .in1(1'b0), .out(save), .sel(HALT));
  Multiplexer #(.enable("false")) multiplexer_3 (.in0(cpu2_1_jr), .in1(1'b0), .out(jr), .sel(HALT));
  Multiplexer #(.enable("false")) multiplexer_4 (.in0(cpu2_1_reddst), .in1(1'b0), .out(RedDst), .sel(HALT));
  Multiplexer #(.enable("false")) multiplexer_5 (.in0(cpu2_1_alusrc), .in1(or_1_out), .out(ALUSrc), .sel(HALT));
  Multiplexer #(.enable("false")) multiplexer_6 (.in0(cpu2_1_memtoreg), .in1(1'b0), .out(memToReg), .sel(HALT));
  Multiplexer #(.enable("false")) multiplexer_7 (.in0(cpu2_1_regwrite), .in1(_2), .out(regWrite), .sel(HALT));
  Multiplexer #(.enable("false")) multiplexer_8 (.in0(cpu2_1_memread), .in1(OUT), .out(memRead), .sel(HALT));
  Multiplexer #(.enable("false")) multiplexer_9 (.in0(cpu2_1_memwrite), .in1(1'b0), .out(memWrite), .sel(HALT));
  Multiplexer #(.enable("false")) multiplexer_10 (.in0(cpu2_1_branch), .in1(1'b0), .out(Branch), .sel(HALT));
  Multiplexer #(.enable("false")) multiplexer_11 (.in0(cpu2_1_aluop1), .in1(1'b0), .out(ALUop1), .sel(HALT));
  Multiplexer #(.enable("false")) multiplexer_12 (.in0(cpu2_1_aluop0), .in1(_0), .out(ALUop0), .sel(HALT));
  Multiplexer #(.enable("false")) multiplexer_13 (.in0(cpu2_1_jump), .in1(1'b0), .out(Jump), .sel(HALT));
  Multiplexer #(.width(2), .enable("false")) multiplexer_14 (
    .in0(2'b00), .in1(multiplexer_1_out), .out(ALU_A), .sel(HALT));
  and and_1 (and_1_out, s_r_ff_1_q, _100100, s_r_ff_2_q);
  and and_2 (and_2_out, s_r_ff_1_qn, ZERO, s_r_ff_2_qn);
  not not_1 (not_1_out, ZERO);
  and and_3 (and_3_out, s_r_ff_2_qn, s_r_ff_1_qn, not_1_out);
  and and_4 (and_4_out, s_r_ff_1_qn, s_r_ff_2_q);
  or or_2 (or_2_out, and_2_out, and_4_out);
  S_R_Flip_Flop s_r_ff_1 (
    .S(or_2_out), .clk(CLOCK), .R(or_3_out), .Q(s_r_ff_1_q), .Qn(s_r_ff_1_qn), .preset(RESET), .en(CLOCK));  // open: reset
  or or_3 (or_3_out, and_5_out, and_3_out, and_1_out);
  and and_5 (and_5_out, s_r_ff_1_q, s_r_ff_2_qn);
  or or_4 (or_4_out, and_2_out, and_3_out);
  S_R_Flip_Flop s_r_ff_2 (
    .S(or_4_out), .clk(CLOCK), .R(or_5_out), .Q(s_r_ff_2_q), .Qn(s_r_ff_2_qn), .preset(RESET), .en(CLOCK));  // open: reset
  or or_5 (or_5_out, and_5_out, and_4_out, and_1_out);
  and u__2 (_2, s_r_ff_1_q, s_r_ff_2_qn);
  and _1 (OUT, s_r_ff_1_qn, s_r_ff_2_q);
  and u__0 (_0, s_r_ff_1_qn, s_r_ff_2_qn);
  or or_6 (HALT, _2, OUT, _0);

  // Other names for the same wires on the sheet: _1 = OUT; seq = HALT

  // Notes on the sheet:
  //   ESTE EN LA ENTRADA DE PC
  //   1/0
  //   msb
endmodule
